// Logisim project project.circ as structural Verilog: 32 circuits, main circuit MAIN
module main (
  input  [6:0] moving,
  input  initgame,
  output [31:0] out_3,
  output [31:0] out_4,
  output [31:0] out_5,
  output [31:0] out_6,
  output [31:0] out_7,
  output [31:0] out_8,
  output [31:0] out_9,
  output [31:0] out_10,
  output [31:0] out_11,
  output [31:0] out_12,
  output [31:0] out_13,
  output [31:0] out_14,
  output [31:0] out_15,
  output [31:0] out_16,
  output [31:0] out_17,
  output [31:0] out_18,
  output [31:0] out_19,
  output [31:0] out_20,
  output [31:0] out_21,
  output [31:0] out_22,
  output [31:0] out_23,
  output [31:0] out_24,
  output [31:0] out_25,
  output [31:0] out_26,
  output [31:0] out_27,
  output [31:0] out_28,
  output [31:0] out_29,
  output [31:0] out_30,
  output [31:0] out_31,
  output [31:0] out_32,
  output [31:0] out_33,
  output [31:0] out_34
);

  wire _1_prime_prime_prime, _2_prime_prime_prime, _3_prime_prime_prime, _4_prime_prime_prime,
       _11_prime_prime_prime, _12_prime_prime_prime, _13_prime_prime_prime, _14_prime_prime_prime,
       clock_1_out, comparator_1_eq, comparator_2_eq, comparator_3_eq;
  wire [4:0] player_move_1_counter;
  wire [7:0] _1_prime, _1_prime_prime, _2_prime, _2_prime_prime, _3_prime, _3_prime_prime, _4_prime,
       _4_prime_prime, register_1_q, register_2_q, register_3_q, register_4_q, register_5_q, register_6_q,
       register_7_q, register_8_q, register_9_q, register_10_q, register_11_q, register_12_q, register_13_q,
       register_14_q, register_15_q, register_16_q, register_33_q;
  wire [31:0] pull_resistor_1_node, pull_resistor_2_node, register_20_q, register_21_q, register_25_q,
       register_29_q, \стенки_1_walls , \стрельба_1_out_4 , \стрельба_1_out_5 , \стрельба_1_out_6 ,
       \стрельба_1_out_7 , \стрельба_1_out_8 , \стрельба_1_out_9 , \стрельба_1_out_10 , \стрельба_1_out_11 ,
       \стрельба_1_out_12 , \стрельба_1_out_13 , \стрельба_1_out_14 , \стрельба_1_out_15 ,
       \стрельба_1_out_16 , \стрельба_1_out_17 , \стрельба_1_out_18 , \стрельба_1_out_19 ,
       \стрельба_1_out_20 , \стрельба_1_out_21 , \стрельба_1_out_22 , \стрельба_1_out_23 ,
       \стрельба_1_out_24 , \стрельба_1_out_25 , \стрельба_1_out_26 , \стрельба_1_out_27 ,
       \стрельба_1_out_28 , \стрельба_1_out_29 , \стрельба_1_out_30 , \стрельба_1_out_31 ,
       \стрельба_1_out_32 , \стрельба_1_out_33 ;

  Register register_1 (.D(_3_prime), .en(initgame), .Q(register_1_q), .clk(initgame), .clr(_1_prime_prime_prime));
  Register register_2 (.D(_3_prime), .en(initgame), .Q(register_2_q), .clk(initgame), .clr(_11_prime_prime_prime));
  Register register_3 (.D(_3_prime_prime), .en(initgame), .Q(register_3_q), .clk(initgame), .clr(_2_prime_prime_prime));
  Register register_4 (
    .D(_3_prime_prime), .en(initgame), .Q(register_4_q), .clk(initgame), .clr(_12_prime_prime_prime));
  Register register_5 (.D(_4_prime), .en(initgame), .Q(register_5_q), .clk(initgame), .clr(_4_prime_prime_prime));
  Register register_6 (.D(_4_prime_prime), .en(initgame), .Q(register_6_q), .clk(initgame), .clr(_3_prime_prime_prime));
  Register register_7 (.D(_4_prime_prime), .en(initgame), .Q(register_7_q), .clk(initgame), .clr(_2_prime_prime_prime));
  Register register_8 (.D(_4_prime), .en(initgame), .Q(register_8_q), .clk(initgame), .clr(_1_prime_prime_prime));
  \монстр__майн  \u_монстр_майн_1  (
    .\_4строка (_4_prime_prime), .\_3строка (_3_prime_prime), .\_2строка (_2_prime_prime),
    .\_1строка (_1_prime_prime));
  Register register_9 (.D(_3_prime_prime), .en(initgame), .Q(register_9_q), .clk(initgame), .clr(_3_prime_prime_prime));
  Register register_10 (
    .D(_3_prime_prime), .en(initgame), .Q(register_10_q), .clk(initgame), .clr(_13_prime_prime_prime));
  Register register_11 (.D(_3_prime), .en(initgame), .Q(register_11_q), .clk(initgame), .clr(_4_prime_prime_prime));
  Register register_12 (.D(_3_prime), .en(initgame), .Q(register_12_q), .clk(initgame), .clr(_14_prime_prime_prime));
  Register register_13 (.D(_4_prime), .en(initgame), .Q(register_13_q), .clk(initgame), .clr(_14_prime_prime_prime));
  Register register_14 (
    .D(_4_prime_prime), .en(initgame), .Q(register_14_q), .clk(initgame), .clr(_13_prime_prime_prime));
  Register register_15 (
    .D(_4_prime_prime), .en(initgame), .Q(register_15_q), .clk(initgame), .clr(_12_prime_prime_prime));
  Register register_16 (.D(_4_prime), .en(initgame), .Q(register_16_q), .clk(initgame), .clr(_11_prime_prime_prime));
  Pull_Resistor pull_resistor_1 (.node(pull_resistor_1_node));
  \монстр__т  \u_монстр_т_1  (
    .\_4строка (_4_prime), .\_3строка (_3_prime), .\_2строка (_2_prime), .\_1строка (_1_prime));
  Clock clock_1 (.out(clock_1_out));
  \стенки  \u_стенки_1  (
    .initwalls(initgame), .bullets(pull_resistor_1_node), .walls(\стенки_1_walls ), .clock(clock_1_out));
  Register register_17 (
    .D(_2_prime), .en(initgame), .Q(register_20_q[7:0]), .clk(initgame), .clr(_14_prime_prime_prime));
  Register register_18 (
    .D(_2_prime_prime), .en(initgame), .Q(register_20_q[15:8]), .clk(initgame), .clr(_13_prime_prime_prime));
  Register register_19 (
    .D(_2_prime_prime), .en(initgame), .Q(register_20_q[23:16]), .clk(initgame), .clr(_12_prime_prime_prime));
  Register register_20 (
    .D(_2_prime), .en(initgame), .Q(register_20_q[31:24]), .clk(initgame), .clr(_11_prime_prime_prime));
  // Probe on moving
  Register register_21 (
    .D(_2_prime), .en(initgame), .Q(register_21_q[7:0]), .clk(initgame), .clr(_4_prime_prime_prime));
  Register register_22 (
    .D(_2_prime_prime), .en(initgame), .Q(register_21_q[15:8]), .clk(initgame), .clr(_3_prime_prime_prime));
  Register register_23 (
    .D(_2_prime_prime), .en(initgame), .Q(register_21_q[23:16]), .clk(initgame), .clr(_2_prime_prime_prime));
  Register register_24 (
    .D(_2_prime), .en(initgame), .Q(register_21_q[31:24]), .clk(initgame), .clr(_1_prime_prime_prime));
  Pull_Resistor pull_resistor_2 (.node(pull_resistor_2_node));
  Player_Move player_move_1 (
    .in_1(comparator_2_eq), .in_2(comparator_1_eq), ._0(out_3), ._1(out_4), .counter(player_move_1_counter));
  Comparator #(.width(7), .mode("unsigned")) comparator_1 (
    .a(moving), .b(7'b1100001), .eq(comparator_1_eq));  // open: gt, lt
  Comparator #(.width(7), .mode("unsigned")) comparator_2 (
    .a(moving), .b(7'b1100100), .eq(comparator_2_eq));  // open: gt, lt
  Comparator #(.width(7), .mode("unsigned")) comparator_3 (
    .a(moving), .b(7'b0100000), .eq(comparator_3_eq));  // open: gt, lt
  Register register_25 (
    .D(_1_prime), .en(initgame), .Q(register_25_q[7:0]), .clk(initgame), .clr(_14_prime_prime_prime));
  Register register_26 (
    .D(_1_prime_prime), .en(initgame), .Q(register_25_q[15:8]), .clk(initgame), .clr(_13_prime_prime_prime));
  Register register_27 (
    .D(_1_prime_prime), .en(initgame), .Q(register_25_q[23:16]), .clk(initgame), .clr(_12_prime_prime_prime));
  Register register_28 (
    .D(_1_prime), .en(initgame), .Q(register_25_q[31:24]), .clk(initgame), .clr(_11_prime_prime_prime));
  Register register_29 (
    .D(_1_prime), .en(initgame), .Q(register_29_q[7:0]), .clk(initgame), .clr(_4_prime_prime_prime));
  Register register_30 (
    .D(_1_prime_prime), .en(initgame), .Q(register_29_q[15:8]), .clk(initgame), .clr(_3_prime_prime_prime));
  Register register_31 (
    .D(_1_prime_prime), .en(initgame), .Q(register_29_q[23:16]), .clk(initgame), .clr(_2_prime_prime_prime));
  Register register_32 (
    .D(_1_prime), .en(initgame), .Q(register_29_q[31:24]), .clk(initgame), .clr(_1_prime_prime_prime));
  \стрельба  \u_стрельба_1  (
    .out_4(\стрельба_1_out_4 ), .out_5(\стрельба_1_out_5 ), .out_6(\стрельба_1_out_6 ),
    .coord(player_move_1_counter), .out_7(\стрельба_1_out_7 ), .out_8(\стрельба_1_out_8 ),
    .out_9(\стрельба_1_out_9 ), .fire(comparator_3_eq), .out_10(\стрельба_1_out_10 ),
    .out_11(\стрельба_1_out_11 ), .out_12(\стрельба_1_out_12 ), .out_13(\стрельба_1_out_13 ),
    .out_14(\стрельба_1_out_14 ), .out_15(\стрельба_1_out_15 ), .out_16(\стрельба_1_out_16 ),
    .out_17(\стрельба_1_out_17 ), .out_18(\стрельба_1_out_18 ), .out_19(\стрельба_1_out_19 ),
    .out_20(\стрельба_1_out_20 ), .out_21(\стрельба_1_out_21 ), .out_22(\стрельба_1_out_22 ),
    .out_23(\стрельба_1_out_23 ), .out_24(\стрельба_1_out_24 ), .out_25(\стрельба_1_out_25 ),
    .out_26(\стрельба_1_out_26 ), .out_27(\стрельба_1_out_27 ), .out_28(\стрельба_1_out_28 ),
    .out_29(\стрельба_1_out_29 ), .out_30(\стрельба_1_out_30 ), .out_31(\стрельба_1_out_31 ),
    .out_32(\стрельба_1_out_32 ), .out_33(\стрельба_1_out_33 ), .clk(clock_1_out));
  Register register_33 (.Q(register_33_q));  // open: D, en, clk, clr
  dtriglit dtriglit_1 (.in(register_33_q[0]), .out(_1_prime_prime_prime));
  dtriglit dtriglit_2 (.in(register_33_q[1]), .out(_2_prime_prime_prime));
  dtriglit dtriglit_3 (.in(register_33_q[2]), .out(_3_prime_prime_prime));
  dtriglit dtriglit_4 (.in(register_33_q[3]), .out(_4_prime_prime_prime));
  dtriglit dtriglit_5 (.in(register_33_q[4]), .out(_11_prime_prime_prime));
  dtriglit dtriglit_6 (.in(register_33_q[5]), .out(_12_prime_prime_prime));
  dtriglit dtriglit_7 (.in(register_33_q[6]), .out(_13_prime_prime_prime));
  dtriglit dtriglit_8 (.in(register_33_q[7]), .out(_14_prime_prime_prime));
  assign out_34 = \стрельба_1_out_33  | register_29_q;  // OR_Gate or_1, 32 bits wide
  assign out_33 = \стрельба_1_out_32  | register_21_q;  // OR_Gate or_2, 32 bits wide
  assign out_32 = \стрельба_1_out_31  | {register_1_q, register_3_q, register_9_q, register_11_q};  // OR_Gate or_3, 32 bits wide
  assign out_31 = \стрельба_1_out_30  | {register_8_q, register_7_q, register_6_q, register_5_q};  // OR_Gate or_4, 32 bits wide
  assign out_30 = \стрельба_1_out_29  | pull_resistor_2_node;  // OR_Gate or_5, 32 bits wide
  assign out_29 = \стрельба_1_out_28  | register_25_q;  // OR_Gate or_6, 32 bits wide
  assign out_28 = \стрельба_1_out_27  | register_20_q;  // OR_Gate or_7, 32 bits wide
  assign out_27 = \стрельба_1_out_26  | {register_2_q, register_4_q, register_10_q, register_12_q};  // OR_Gate or_8, 32 bits wide
  assign out_26 = \стрельба_1_out_25  | {register_16_q, register_15_q, register_14_q, register_13_q};  // OR_Gate or_9, 32 bits wide
  assign out_25 = \стрельба_1_out_24  | pull_resistor_2_node;  // OR_Gate or_10, 32 bits wide
  assign out_24 = \стрельба_1_out_23  | pull_resistor_2_node;  // OR_Gate or_11, 32 bits wide
  assign out_23 = \стрельба_1_out_22  | pull_resistor_2_node;  // OR_Gate or_12, 32 bits wide
  assign out_22 = \стрельба_1_out_21  | pull_resistor_2_node;  // OR_Gate or_13, 32 bits wide
  assign out_21 = \стрельба_1_out_20  | pull_resistor_2_node;  // OR_Gate or_14, 32 bits wide
  assign out_20 = \стрельба_1_out_19  | pull_resistor_2_node;  // OR_Gate or_15, 32 bits wide
  assign out_19 = \стрельба_1_out_18  | pull_resistor_2_node;  // OR_Gate or_16, 32 bits wide
  assign out_18 = \стрельба_1_out_17  | pull_resistor_2_node;  // OR_Gate or_17, 32 bits wide
  assign out_17 = \стрельба_1_out_16  | pull_resistor_2_node;  // OR_Gate or_18, 32 bits wide
  assign out_16 = \стрельба_1_out_15  | pull_resistor_2_node;  // OR_Gate or_19, 32 bits wide
  assign out_15 = \стрельба_1_out_14  | pull_resistor_2_node;  // OR_Gate or_20, 32 bits wide
  assign out_14 = \стрельба_1_out_13  | pull_resistor_2_node;  // OR_Gate or_21, 32 bits wide
  assign out_13 = \стрельба_1_out_12  | pull_resistor_2_node;  // OR_Gate or_22, 32 bits wide
  assign out_12 = \стрельба_1_out_11  | pull_resistor_2_node;  // OR_Gate or_23, 32 bits wide
  assign out_11 = \стрельба_1_out_10  | pull_resistor_2_node;  // OR_Gate or_24, 32 bits wide
  assign out_10 = \стрельба_1_out_9  | pull_resistor_2_node;  // OR_Gate or_25, 32 bits wide
  assign out_9 = \стрельба_1_out_8  | pull_resistor_2_node;  // OR_Gate or_26, 32 bits wide
  assign out_8 = \стрельба_1_out_7  | pull_resistor_2_node;  // OR_Gate or_27, 32 bits wide
  assign out_7 = \стрельба_1_out_6  | pull_resistor_2_node;  // OR_Gate or_28, 32 bits wide
  assign out_6 = \стрельба_1_out_5  | pull_resistor_2_node;  // OR_Gate or_29, 32 bits wide
  assign out_5 = \стрельба_1_out_4  | \стенки_1_walls ;  // OR_Gate or_30, 32 bits wide

  // Other names for the same wires on the sheet: _0[31:0] = out_3; _1[31:0] = out_4; _2[31:0] = out_5;
  //   _3[31:0] = out_6; _4[31:0] = out_7; _5[31:0] = out_8; _6[31:0] = out_9; _7[31:0] = out_10; _8[31:0] = out_11;
  //   _9[31:0] = out_12; _10[31:0] = out_13; _11[31:0] = out_14; _12[31:0] = out_15; _13[31:0] = out_16;
  //   _14[31:0] = out_17; _15[31:0] = out_18; _16[31:0] = out_19; _17[31:0] = out_20; _18[31:0] = out_21;
  //   _19[31:0] = out_22; _20[31:0] = out_23; _21[31:0] = out_24; _22[31:0] = out_25; _23[31:0] = out_26;
  //   _24[31:0] = out_27; _25[31:0] = out_28; _26[31:0] = out_29; _27[31:0] = out_30; _28[31:0] = out_31;
  //   _29[31:0] = out_32; _30[31:0] = out_33; _31[31:0] = out_34; init = initgame
endmodule

module inc5 (
  input  [4:0] X,
  output [4:0] R,
  output Cout
);

  wire [4:1] and_1_out;

  assign {Cout, and_1_out} = {and_1_out, 1'b1} & X;  // AND_Gate and_1, 5 bits wide
  assign R = X ^ {and_1_out, 1'b1};  // XOR_Gate xor_1, 5 bits wide
endmodule

module dec8 (
  input  [7:0] X,
  output [7:0] R,
  output Cout
);

  wire [7:1] and_1_out;
  wire [7:7] and_1_out_2;

  assign R = ~(X ^ ~{and_1_out, 1'b1});  // XNOR_Gate xnor_1, 8 bits wide
  assign {and_1_out_2[7], and_1_out} = ~X & {and_1_out, 1'b1};  // AND_Gate and_1, 8 bits wide
  Multiplexer #(.disabled(0), .enable("false")) multiplexer_1 (
    .in0(1'b1), .in1(1'b0), .out(Cout), .sel(and_1_out_2[7]));
endmodule

module T_Block (
  input  A,
  input  B,
  input  C,
  output OUT
);

  or or_1 (OUT, A, B, C);
endmodule

module Player_Move (
  input  in_1,
  input  in_2,
  output [4:0] counter,
  output [31:0] _0,
  output [31:0] _1
);

  wire or_1_out;
  wire [31:5] counter_1_q;

  T_Block t_block_1 (.A(_1[22]), .B(_1[24]), .C(_1[23]), .OUT(_0[23]));
  T_Block t_block_2 (.A(_1[21]), .B(_1[23]), .C(_1[22]), .OUT(_0[22]));
  T_Block t_block_3 (.A(_1[20]), .B(_1[22]), .C(_1[21]), .OUT(_0[21]));
  T_Block t_block_4 (.A(_1[19]), .B(_1[21]), .C(_1[20]), .OUT(_0[20]));
  T_Block t_block_5 (.A(_1[18]), .B(_1[20]), .C(_1[19]), .OUT(_0[19]));
  T_Block t_block_6 (.A(_1[17]), .B(_1[19]), .C(_1[18]), .OUT(_0[18]));
  T_Block t_block_7 (.A(_1[31]), .B(_1[1]), .C(_1[0]), .OUT(_0[0]));
  T_Block t_block_8 (.A(_1[16]), .B(_1[18]), .C(_1[17]), .OUT(_0[17]));
  T_Block t_block_9 (.A(_1[0]), .B(_1[2]), .C(_1[1]), .OUT(_0[1]));
  T_Block t_block_10 (.A(_1[1]), .B(_1[3]), .C(_1[2]), .OUT(_0[2]));
  T_Block t_block_11 (.A(_1[15]), .B(_1[17]), .C(_1[16]), .OUT(_0[16]));
  T_Block t_block_12 (.A(_1[2]), .B(_1[4]), .C(_1[3]), .OUT(_0[3]));
  T_Block t_block_13 (.A(_1[3]), .B(_1[5]), .C(_1[4]), .OUT(_0[4]));
  T_Block t_block_14 (.A(_1[14]), .B(_1[16]), .C(_1[15]), .OUT(_0[15]));
  T_Block t_block_15 (.A(_1[13]), .B(_1[15]), .C(_1[14]), .OUT(_0[14]));
  T_Block t_block_16 (.A(_1[12]), .B(_1[14]), .C(_1[13]), .OUT(_0[13]));
  T_Block t_block_17 (.A(_1[11]), .B(_1[13]), .C(_1[12]), .OUT(_0[12]));
  T_Block t_block_18 (.A(_1[10]), .B(_1[12]), .C(_1[11]), .OUT(_0[11]));
  T_Block t_block_19 (.A(_1[9]), .B(_1[11]), .C(_1[10]), .OUT(_0[10]));
  T_Block t_block_20 (.A(_1[8]), .B(_1[10]), .C(_1[9]), .OUT(_0[9]));
  T_Block t_block_21 (.A(_1[7]), .B(_1[9]), .C(_1[8]), .OUT(_0[8]));
  T_Block t_block_22 (.A(_1[4]), .B(_1[6]), .C(_1[5]), .OUT(_0[5]));
  T_Block t_block_23 (.A(_1[5]), .B(_1[6]), .C(_1[7]), .OUT(_0[6]));
  T_Block t_block_24 (.A(_1[25]), .B(_1[24]), .C(_1[23]), .OUT(_0[24]));
  T_Block t_block_25 (.A(_1[26]), .B(_1[25]), .C(_1[27]), .OUT(_0[26]));
  T_Block t_block_26 (.A(_1[27]), .B(_1[26]), .C(_1[28]), .OUT(_0[27]));
  T_Block t_block_27 (.A(_1[28]), .B(_1[27]), .C(_1[29]), .OUT(_0[28]));
  T_Block t_block_28 (.A(_1[31]), .B(_1[29]), .C(_1[30]), .OUT(_0[30]));
  T_Block t_block_29 (.A(_1[31]), .B(_1[30]), .C(_1[0]), .OUT(_0[31]));
  T_Block t_block_30 (.A(_1[25]), .B(_1[24]), .C(_1[26]), .OUT(_0[25]));
  T_Block t_block_31 (.A(_1[30]), .B(_1[29]), .C(_1[28]), .OUT(_0[29]));
  T_Block t_block_32 (.A(_1[6]), .B(_1[7]), .C(_1[8]), .OUT(_0[7]));
  or or_1 (or_1_out, in_1, in_2);
  Counter #(.width(32), .max('h1f)) counter_1 (
    .load(in_1), .Q({counter_1_q, counter}), .clk(or_1_out));  // open: D, count, carry, clr
  Shifter #(.width(32), .shift("rl")) shifter_1 (.in(32'h1), .\dist (counter), .out(_1));
endmodule

module \монстр__т  (
  output [7:0] \_4строка ,
  output [7:0] \_3строка ,
  output [7:0] \_2строка ,
  output [7:0] \_1строка 
);

  DotMatrix #(.inputtype("row"), .matrixcols(8), .matrixrows(4)) dotmatrix_1 (
    .row0(8'h24), .row1(8'h18), .row2(8'h5a), .row3(8'h24));

  assign \_1строка  = 8'h24;
  assign \_2строка  = 8'h5a;
  assign \_3строка  = 8'h18;
  assign \_4строка  = 8'h24;
endmodule

module \монстр__майн  (
  output [7:0] \_4строка ,
  output [7:0] \_3строка ,
  output [7:0] \_2строка ,
  output [7:0] \_1строка 
);

  DotMatrix #(.inputtype("row"), .matrixcols(8), .matrixrows(4)) dotmatrix_1 (
    .row0(8'h24), .row1(8'h18), .row2(8'h24), .row3(8'h18));

  assign \_1строка  = 8'h18;
  assign \_2строка  = 8'h24;
  assign \_3строка  = 8'h18;
  assign \_4строка  = 8'h24;
endmodule

module \Перевернуть  (
  input  [31:0] in_1,
  output [31:0] out_2
);


  assign out_2 = {in_1[0], in_1[1], in_1[2], in_1[3], in_1[4], in_1[5], in_1[6], in_1[7], in_1[8], in_1[9], in_1[10], in_1[11], in_1[12], in_1[13], in_1[14], in_1[15], in_1[16], in_1[17], in_1[18], in_1[19], in_1[20], in_1[21], in_1[22], in_1[23], in_1[24], in_1[25], in_1[26], in_1[27], in_1[28], in_1[29], in_1[30], in_1[31]};
endmodule

module transpon (
  input  [31:0] in_1,
  input  [31:0] in_2,
  input  [31:0] in_3,
  input  [31:0] in_4,
  input  [31:0] in_5,
  input  [31:0] in_6,
  input  [31:0] in_7,
  input  [31:0] in_8,
  input  [31:0] in_9,
  input  [31:0] in_10,
  input  [31:0] in_11,
  input  [31:0] in_12,
  input  [31:0] in_13,
  input  [31:0] in_14,
  input  [31:0] in_15,
  input  [31:0] in_16,
  input  [31:0] in_17,
  input  [31:0] in_18,
  input  [31:0] in_19,
  input  [31:0] in_20,
  input  [31:0] in_21,
  input  [31:0] in_22,
  input  [31:0] in_23,
  input  [31:0] in_24,
  input  [31:0] in_25,
  input  [31:0] in_26,
  input  [31:0] in_27,
  input  [31:0] in_28,
  input  [31:0] in_29,
  input  [31:0] in_30,
  input  [31:0] in_31,
  input  [31:0] in_32,
  output [31:0] _0,
  output [31:0] _1,
  output [31:0] _2,
  output [31:0] _3,
  output [31:0] _4,
  output [31:0] _5,
  output [31:0] _6,
  output [31:0] _7,
  output [31:0] _8,
  output [31:0] _9,
  output [31:0] _10,
  output [31:0] _11,
  output [31:0] _12,
  output [31:0] _13,
  output [31:0] _14,
  output [31:0] _15,
  output [31:0] _16,
  output [31:0] _17,
  output [31:0] _18,
  output [31:0] _19,
  output [31:0] _20,
  output [31:0] _21,
  output [31:0] _22,
  output [31:0] _23,
  output [31:0] _24,
  output [31:0] _25,
  output [31:0] _26,
  output [31:0] _27,
  output [31:0] _28,
  output [31:0] _29,
  output [31:0] _30,
  output [31:0] _31
);

  \Перевернуть  \u_перевернуть_1  (
    .in_1({in_32[0], in_31[0], in_30[0], in_29[0], in_28[0], in_27[0], in_26[0], in_25[0], in_24[0], in_23[0], in_22[0], in_21[0], in_20[0], in_19[0], in_18[0], in_17[0], in_16[0], in_15[0], in_14[0], in_13[0], in_12[0], in_11[0], in_10[0], in_9[0], in_8[0], in_7[0], in_6[0], in_5[0], in_4[0], in_3[0], in_2[0], in_1[0]}),
    .out_2(_0));
  \Перевернуть  \u_перевернуть_2  (
    .in_1({in_32[4], in_31[4], in_30[4], in_29[4], in_28[4], in_27[4], in_26[4], in_25[4], in_24[4], in_23[4], in_22[4], in_21[4], in_20[4], in_19[4], in_18[4], in_17[4], in_16[4], in_15[4], in_14[4], in_13[4], in_12[4], in_11[4], in_10[4], in_9[4], in_8[4], in_7[4], in_6[4], in_5[4], in_4[4], in_3[4], in_2[4], in_1[4]}),
    .out_2(_4));
  \Перевернуть  \u_перевернуть_3  (
    .in_1({in_32[8], in_31[8], in_30[8], in_29[8], in_28[8], in_27[8], in_26[8], in_25[8], in_24[8], in_23[8], in_22[8], in_21[8], in_20[8], in_19[8], in_18[8], in_17[8], in_16[8], in_15[8], in_14[8], in_13[8], in_12[8], in_11[8], in_10[8], in_9[8], in_8[8], in_7[8], in_6[8], in_5[8], in_4[8], in_3[8], in_2[8], in_1[8]}),
    .out_2(_8));
  \Перевернуть  \u_перевернуть_4  (
    .in_1({in_32[12], in_31[12], in_30[12], in_29[12], in_28[12], in_27[12], in_26[12], in_25[12], in_24[12], in_23[12], in_22[12], in_21[12], in_20[12], in_19[12], in_18[12], in_17[12], in_16[12], in_15[12], in_14[12], in_13[12], in_12[12], in_11[12], in_10[12], in_9[12], in_8[12], in_7[12], in_6[12], in_5[12], in_4[12], in_3[12], in_2[12], in_1[12]}),
    .out_2(_12));
  \Перевернуть  \u_перевернуть_5  (
    .in_1({in_32[16], in_31[16], in_30[16], in_29[16], in_28[16], in_27[16], in_26[16], in_25[16], in_24[16], in_23[16], in_22[16], in_21[16], in_20[16], in_19[16], in_18[16], in_17[16], in_16[16], in_15[16], in_14[16], in_13[16], in_12[16], in_11[16], in_10[16], in_9[16], in_8[16], in_7[16], in_6[16], in_5[16], in_4[16], in_3[16], in_2[16], in_1[16]}),
    .out_2(_16));
  \Перевернуть  \u_перевернуть_6  (
    .in_1({in_32[20], in_31[20], in_30[20], in_29[20], in_28[20], in_27[20], in_26[20], in_25[20], in_24[20], in_23[20], in_22[20], in_21[20], in_20[20], in_19[20], in_18[20], in_17[20], in_16[20], in_15[20], in_14[20], in_13[20], in_12[20], in_11[20], in_10[20], in_9[20], in_8[20], in_7[20], in_6[20], in_5[20], in_4[20], in_3[20], in_2[20], in_1[20]}),
    .out_2(_20));
  \Перевернуть  \u_перевернуть_7  (
    .in_1({in_32[24], in_31[24], in_30[24], in_29[24], in_28[24], in_27[24], in_26[24], in_25[24], in_24[24], in_23[24], in_22[24], in_21[24], in_20[24], in_19[24], in_18[24], in_17[24], in_16[24], in_15[24], in_14[24], in_13[24], in_12[24], in_11[24], in_10[24], in_9[24], in_8[24], in_7[24], in_6[24], in_5[24], in_4[24], in_3[24], in_2[24], in_1[24]}),
    .out_2(_24));
  \Перевернуть  \u_перевернуть_8  (
    .in_1({in_32[28], in_31[28], in_30[28], in_29[28], in_28[28], in_27[28], in_26[28], in_25[28], in_24[28], in_23[28], in_22[28], in_21[28], in_20[28], in_19[28], in_18[28], in_17[28], in_16[28], in_15[28], in_14[28], in_13[28], in_12[28], in_11[28], in_10[28], in_9[28], in_8[28], in_7[28], in_6[28], in_5[28], in_4[28], in_3[28], in_2[28], in_1[28]}),
    .out_2(_28));
  \Перевернуть  \u_перевернуть_9  (
    .in_1({in_32[1], in_31[1], in_30[1], in_29[1], in_28[1], in_27[1], in_26[1], in_25[1], in_24[1], in_23[1], in_22[1], in_21[1], in_20[1], in_19[1], in_18[1], in_17[1], in_16[1], in_15[1], in_14[1], in_13[1], in_12[1], in_11[1], in_10[1], in_9[1], in_8[1], in_7[1], in_6[1], in_5[1], in_4[1], in_3[1], in_2[1], in_1[1]}),
    .out_2(_1));
  \Перевернуть  \u_перевернуть_10  (
    .in_1({in_32[5], in_31[5], in_30[5], in_29[5], in_28[5], in_27[5], in_26[5], in_25[5], in_24[5], in_23[5], in_22[5], in_21[5], in_20[5], in_19[5], in_18[5], in_17[5], in_16[5], in_15[5], in_14[5], in_13[5], in_12[5], in_11[5], in_10[5], in_9[5], in_8[5], in_7[5], in_6[5], in_5[5], in_4[5], in_3[5], in_2[5], in_1[5]}),
    .out_2(_5));
  \Перевернуть  \u_перевернуть_11  (
    .in_1({in_32[9], in_31[9], in_30[9], in_29[9], in_28[9], in_27[9], in_26[9], in_25[9], in_24[9], in_23[9], in_22[9], in_21[9], in_20[9], in_19[9], in_18[9], in_17[9], in_16[9], in_15[9], in_14[9], in_13[9], in_12[9], in_11[9], in_10[9], in_9[9], in_8[9], in_7[9], in_6[9], in_5[9], in_4[9], in_3[9], in_2[9], in_1[9]}),
    .out_2(_9));
  \Перевернуть  \u_перевернуть_12  (
    .in_1({in_32[13], in_31[13], in_30[13], in_29[13], in_28[13], in_27[13], in_26[13], in_25[13], in_24[13], in_23[13], in_22[13], in_21[13], in_20[13], in_19[13], in_18[13], in_17[13], in_16[13], in_15[13], in_14[13], in_13[13], in_12[13], in_11[13], in_10[13], in_9[13], in_8[13], in_7[13], in_6[13], in_5[13], in_4[13], in_3[13], in_2[13], in_1[13]}),
    .out_2(_13));
  \Перевернуть  \u_перевернуть_13  (
    .in_1({in_32[17], in_31[17], in_30[17], in_29[17], in_28[17], in_27[17], in_26[17], in_25[17], in_24[17], in_23[17], in_22[17], in_21[17], in_20[17], in_19[17], in_18[17], in_17[17], in_16[17], in_15[17], in_14[17], in_13[17], in_12[17], in_11[17], in_10[17], in_9[17], in_8[17], in_7[17], in_6[17], in_5[17], in_4[17], in_3[17], in_2[17], in_1[17]}),
    .out_2(_17));
  \Перевернуть  \u_перевернуть_14  (
    .in_1({in_32[21], in_31[21], in_30[21], in_29[21], in_28[21], in_27[21], in_26[21], in_25[21], in_24[21], in_23[21], in_22[21], in_21[21], in_20[21], in_19[21], in_18[21], in_17[21], in_16[21], in_15[21], in_14[21], in_13[21], in_12[21], in_11[21], in_10[21], in_9[21], in_8[21], in_7[21], in_6[21], in_5[21], in_4[21], in_3[21], in_2[21], in_1[21]}),
    .out_2(_21));
  \Перевернуть  \u_перевернуть_15  (
    .in_1({in_32[25], in_31[25], in_30[25], in_29[25], in_28[25], in_27[25], in_26[25], in_25[25], in_24[25], in_23[25], in_22[25], in_21[25], in_20[25], in_19[25], in_18[25], in_17[25], in_16[25], in_15[25], in_14[25], in_13[25], in_12[25], in_11[25], in_10[25], in_9[25], in_8[25], in_7[25], in_6[25], in_5[25], in_4[25], in_3[25], in_2[25], in_1[25]}),
    .out_2(_25));
  \Перевернуть  \u_перевернуть_16  (
    .in_1({in_32[29], in_31[29], in_30[29], in_29[29], in_28[29], in_27[29], in_26[29], in_25[29], in_24[29], in_23[29], in_22[29], in_21[29], in_20[29], in_19[29], in_18[29], in_17[29], in_16[29], in_15[29], in_14[29], in_13[29], in_12[29], in_11[29], in_10[29], in_9[29], in_8[29], in_7[29], in_6[29], in_5[29], in_4[29], in_3[29], in_2[29], in_1[29]}),
    .out_2(_29));
  \Перевернуть  \u_перевернуть_17  (
    .in_1({in_32[2], in_31[2], in_30[2], in_29[2], in_28[2], in_27[2], in_26[2], in_25[2], in_24[2], in_23[2], in_22[2], in_21[2], in_20[2], in_19[2], in_18[2], in_17[2], in_16[2], in_15[2], in_14[2], in_13[2], in_12[2], in_11[2], in_10[2], in_9[2], in_8[2], in_7[2], in_6[2], in_5[2], in_4[2], in_3[2], in_2[2], in_1[2]}),
    .out_2(_2));
  \Перевернуть  \u_перевернуть_18  (
    .in_1({in_32[6], in_31[6], in_30[6], in_29[6], in_28[6], in_27[6], in_26[6], in_25[6], in_24[6], in_23[6], in_22[6], in_21[6], in_20[6], in_19[6], in_18[6], in_17[6], in_16[6], in_15[6], in_14[6], in_13[6], in_12[6], in_11[6], in_10[6], in_9[6], in_8[6], in_7[6], in_6[6], in_5[6], in_4[6], in_3[6], in_2[6], in_1[6]}),
    .out_2(_6));
  \Перевернуть  \u_перевернуть_19  (
    .in_1({in_32[10], in_31[10], in_30[10], in_29[10], in_28[10], in_27[10], in_26[10], in_25[10], in_24[10], in_23[10], in_22[10], in_21[10], in_20[10], in_19[10], in_18[10], in_17[10], in_16[10], in_15[10], in_14[10], in_13[10], in_12[10], in_11[10], in_10[10], in_9[10], in_8[10], in_7[10], in_6[10], in_5[10], in_4[10], in_3[10], in_2[10], in_1[10]}),
    .out_2(_10));
  \Перевернуть  \u_перевернуть_20  (
    .in_1({in_32[14], in_31[14], in_30[14], in_29[14], in_28[14], in_27[14], in_26[14], in_25[14], in_24[14], in_23[14], in_22[14], in_21[14], in_20[14], in_19[14], in_18[14], in_17[14], in_16[14], in_15[14], in_14[14], in_13[14], in_12[14], in_11[14], in_10[14], in_9[14], in_8[14], in_7[14], in_6[14], in_5[14], in_4[14], in_3[14], in_2[14], in_1[14]}),
    .out_2(_14));
  \Перевернуть  \u_перевернуть_21  (
    .in_1({in_32[18], in_31[18], in_30[18], in_29[18], in_28[18], in_27[18], in_26[18], in_25[18], in_24[18], in_23[18], in_22[18], in_21[18], in_20[18], in_19[18], in_18[18], in_17[18], in_16[18], in_15[18], in_14[18], in_13[18], in_12[18], in_11[18], in_10[18], in_9[18], in_8[18], in_7[18], in_6[18], in_5[18], in_4[18], in_3[18], in_2[18], in_1[18]}),
    .out_2(_18));
  \Перевернуть  \u_перевернуть_22  (
    .in_1({in_32[22], in_31[22], in_30[22], in_29[22], in_28[22], in_27[22], in_26[22], in_25[22], in_24[22], in_23[22], in_22[22], in_21[22], in_20[22], in_19[22], in_18[22], in_17[22], in_16[22], in_15[22], in_14[22], in_13[22], in_12[22], in_11[22], in_10[22], in_9[22], in_8[22], in_7[22], in_6[22], in_5[22], in_4[22], in_3[22], in_2[22], in_1[22]}),
    .out_2(_22));
  \Перевернуть  \u_перевернуть_23  (
    .in_1({in_32[26], in_31[26], in_30[26], in_29[26], in_28[26], in_27[26], in_26[26], in_25[26], in_24[26], in_23[26], in_22[26], in_21[26], in_20[26], in_19[26], in_18[26], in_17[26], in_16[26], in_15[26], in_14[26], in_13[26], in_12[26], in_11[26], in_10[26], in_9[26], in_8[26], in_7[26], in_6[26], in_5[26], in_4[26], in_3[26], in_2[26], in_1[26]}),
    .out_2(_26));
  \Перевернуть  \u_перевернуть_24  (
    .in_1({in_32[30], in_31[30], in_30[30], in_29[30], in_28[30], in_27[30], in_26[30], in_25[30], in_24[30], in_23[30], in_22[30], in_21[30], in_20[30], in_19[30], in_18[30], in_17[30], in_16[30], in_15[30], in_14[30], in_13[30], in_12[30], in_11[30], in_10[30], in_9[30], in_8[30], in_7[30], in_6[30], in_5[30], in_4[30], in_3[30], in_2[30], in_1[30]}),
    .out_2(_30));
  \Перевернуть  \u_перевернуть_25  (
    .in_1({in_32[3], in_31[3], in_30[3], in_29[3], in_28[3], in_27[3], in_26[3], in_25[3], in_24[3], in_23[3], in_22[3], in_21[3], in_20[3], in_19[3], in_18[3], in_17[3], in_16[3], in_15[3], in_14[3], in_13[3], in_12[3], in_11[3], in_10[3], in_9[3], in_8[3], in_7[3], in_6[3], in_5[3], in_4[3], in_3[3], in_2[3], in_1[3]}),
    .out_2(_3));
  \Перевернуть  \u_перевернуть_26  (
    .in_1({in_32[7], in_31[7], in_30[7], in_29[7], in_28[7], in_27[7], in_26[7], in_25[7], in_24[7], in_23[7], in_22[7], in_21[7], in_20[7], in_19[7], in_18[7], in_17[7], in_16[7], in_15[7], in_14[7], in_13[7], in_12[7], in_11[7], in_10[7], in_9[7], in_8[7], in_7[7], in_6[7], in_5[7], in_4[7], in_3[7], in_2[7], in_1[7]}),
    .out_2(_7));
  \Перевернуть  \u_перевернуть_27  (
    .in_1({in_32[11], in_31[11], in_30[11], in_29[11], in_28[11], in_27[11], in_26[11], in_25[11], in_24[11], in_23[11], in_22[11], in_21[11], in_20[11], in_19[11], in_18[11], in_17[11], in_16[11], in_15[11], in_14[11], in_13[11], in_12[11], in_11[11], in_10[11], in_9[11], in_8[11], in_7[11], in_6[11], in_5[11], in_4[11], in_3[11], in_2[11], in_1[11]}),
    .out_2(_11));
  \Перевернуть  \u_перевернуть_28  (
    .in_1({in_32[15], in_31[15], in_30[15], in_29[15], in_28[15], in_27[15], in_26[15], in_25[15], in_24[15], in_23[15], in_22[15], in_21[15], in_20[15], in_19[15], in_18[15], in_17[15], in_16[15], in_15[15], in_14[15], in_13[15], in_12[15], in_11[15], in_10[15], in_9[15], in_8[15], in_7[15], in_6[15], in_5[15], in_4[15], in_3[15], in_2[15], in_1[15]}),
    .out_2(_15));
  \Перевернуть  \u_перевернуть_29  (
    .in_1({in_32[19], in_31[19], in_30[19], in_29[19], in_28[19], in_27[19], in_26[19], in_25[19], in_24[19], in_23[19], in_22[19], in_21[19], in_20[19], in_19[19], in_18[19], in_17[19], in_16[19], in_15[19], in_14[19], in_13[19], in_12[19], in_11[19], in_10[19], in_9[19], in_8[19], in_7[19], in_6[19], in_5[19], in_4[19], in_3[19], in_2[19], in_1[19]}),
    .out_2(_19));
  \Перевернуть  \u_перевернуть_30  (
    .in_1({in_32[23], in_31[23], in_30[23], in_29[23], in_28[23], in_27[23], in_26[23], in_25[23], in_24[23], in_23[23], in_22[23], in_21[23], in_20[23], in_19[23], in_18[23], in_17[23], in_16[23], in_15[23], in_14[23], in_13[23], in_12[23], in_11[23], in_10[23], in_9[23], in_8[23], in_7[23], in_6[23], in_5[23], in_4[23], in_3[23], in_2[23], in_1[23]}),
    .out_2(_23));
  \Перевернуть  \u_перевернуть_31  (
    .in_1({in_32[27], in_31[27], in_30[27], in_29[27], in_28[27], in_27[27], in_26[27], in_25[27], in_24[27], in_23[27], in_22[27], in_21[27], in_20[27], in_19[27], in_18[27], in_17[27], in_16[27], in_15[27], in_14[27], in_13[27], in_12[27], in_11[27], in_10[27], in_9[27], in_8[27], in_7[27], in_6[27], in_5[27], in_4[27], in_3[27], in_2[27], in_1[27]}),
    .out_2(_27));
  \Перевернуть  \u_перевернуть_32  (
    .in_1({in_32[31], in_31[31], in_30[31], in_29[31], in_28[31], in_27[31], in_26[31], in_25[31], in_24[31], in_23[31], in_22[31], in_21[31], in_20[31], in_19[31], in_18[31], in_17[31], in_16[31], in_15[31], in_14[31], in_13[31], in_12[31], in_11[31], in_10[31], in_9[31], in_8[31], in_7[31], in_6[31], in_5[31], in_4[31], in_3[31], in_2[31], in_1[31]}),
    .out_2(_31));

  // Other names for the same wires on the sheet: _0_t[31:0] = in_1; _1_t[31:0] = in_2; _2_t[31:0] = in_3;
  //   _3_t[31:0] = in_4; _4_t[31:0] = in_5; _5_t[31:0] = in_6; _6_t[31:0] = in_7; _7_t[31:0] = in_8;
  //   _8_t[31:0] = in_9; _9_t[31:0] = in_10; _10_t[31:0] = in_11; _11_t[31:0] = in_12; _12_t[31:0] = in_13;
  //   _13_t[31:0] = in_14; _14_t[31:0] = in_15; _15_t[31:0] = in_16; _16_t[31:0] = in_17; _17_t[31:0] = in_18;
  //   _18_t[31:0] = in_19; _19_t[31:0] = in_20; _20_t[31:0] = in_21; _21_t[31:0] = in_22; _22_t[31:0] = in_23;
  //   _23_t[31:0] = in_24; _24_t[31:0] = in_25; _25_t[31:0] = in_26; _26_t[31:0] = in_27; _27_t[31:0] = in_28;
  //   _28_t[31:0] = in_29; _29_t[31:0] = in_30; _30_t[31:0] = in_31; _31_t[31:0] = in_32
endmodule

module \стенки  (
  input  [31:0] bullets,
  input  initwalls,
  input  clock,
  output [31:0] walls
);

  wire _0, _1, _2, _3, and_3_out, cdm_8_mark5_1_data_inst, cdm_8_mark5_1_mem_cycle, clk1, clk2, clk3,
       comparator_1_gt, comparator_2_lt, d_ff_1_q, d_ff_2_q, d_ff_3_q, d_ff_4_q, decoder_1_out0,
       decoder_1_out1, IAck, IOsel, IRQ, multiplexer_8_out, not_1_out, not_2_out, of1, of2, or_1_out,
       or_2_out, or_3_out, or_4_out, or_5_out, or_6_out, READwrite, reset, resreg, writenow;
  wire [1:0] ctr, index;
  wire [2:0] vec;
  wire [7:0] adress, bulladr, bulldat, cdm_8_mark5_1_data_out, cdm_8_mark5_1_r3, controlled_buffer_2_out,
       demultiplexer_1_out0, demultiplexer_1_out1, demultiplexer_1_out2, demultiplexer_1_out3, IOdat,
       multiplexer_1_out, multiplexer_2_out, multiplexer_3_out, multiplexer_4_out, multiplexer_6_out,
       multiplexer_7_out, walladr, walldat, walls_t;
  wire [7:2] subtractor_1_out;
  wire [31:0] \попадание_1_out ;

  Demultiplexer #(.select(2), .width(8)) demultiplexer_1 (
    .out0(demultiplexer_1_out0), .out1(demultiplexer_1_out1), .out2(demultiplexer_1_out2),
    .out3(demultiplexer_1_out3), .in(walls_t), .sel(index));  // open: en
  \попадание  \u_попадание_1  (.OUT(\попадание_1_out ), .A(walls), .B(bullets));
  \передача_данных  bull (
    .data(\попадание_1_out ), .slowenclock(clk1), .adress(8'h2f), .dataout(bulldat), .adressout(bulladr),
    .of(of1), .res(reset));
  D_Flip_Flop d_ff_1 (.D(of2), .Q(d_ff_1_q), .preset(of2), .reset(reset));  // open: clk, Qn, en
  // Probe on bulldat
  // Probe on bulladr
  Multiplexer #(.width(8)) multiplexer_1 (
    .in0(8'h3c), .in1(demultiplexer_1_out0), .out(multiplexer_1_out), .sel(d_ff_1_q));  // open: en
  Multiplexer #(.width(8)) multiplexer_2 (
    .in0(8'h3c), .in1(demultiplexer_1_out1), .out(multiplexer_2_out), .sel(d_ff_1_q));  // open: en
  Multiplexer #(.width(8)) multiplexer_3 (
    .in0(8'h3c), .in1(demultiplexer_1_out2), .out(multiplexer_3_out), .sel(d_ff_1_q));  // open: en
  Multiplexer #(.width(8)) multiplexer_4 (
    .in0(8'h3c), .in1(demultiplexer_1_out3), .out(multiplexer_4_out), .sel(d_ff_1_q));  // open: en
  or or_1 (or_1_out, \попадание_1_out [0], \попадание_1_out [1], \попадание_1_out [2], \попадание_1_out [3], \попадание_1_out [4], \попадание_1_out [5], \попадание_1_out [6], \попадание_1_out [7], \попадание_1_out [8], \попадание_1_out [9], \попадание_1_out [10], \попадание_1_out [11], \попадание_1_out [12], \попадание_1_out [13], \попадание_1_out [14], \попадание_1_out [15], \попадание_1_out [16], \попадание_1_out [17], \попадание_1_out [18], \попадание_1_out [19], \попадание_1_out [20], \попадание_1_out [21], \попадание_1_out [22], \попадание_1_out [23], \попадание_1_out [24], \попадание_1_out [25], \попадание_1_out [26], \попадание_1_out [27], \попадание_1_out [28], \попадание_1_out [29], \попадание_1_out [30], \попадание_1_out [31]);
  Register #(.trigger("high")) register_1 (
    .D(multiplexer_1_out), .en(or_2_out), .Q(walls[7:0]), .clk(clock));  // open: clr
  or or_2 (or_2_out, initwalls, _0);
  Register #(.trigger("high")) register_2 (
    .D(multiplexer_2_out), .en(or_3_out), .Q(walls[15:8]), .clk(clock));  // open: clr
  or or_3 (or_3_out, initwalls, _1);
  Register #(.trigger("high")) register_3 (
    .D(multiplexer_3_out), .en(or_4_out), .Q(walls[23:16]), .clk(clock));  // open: clr
  or or_4 (or_4_out, initwalls, _2);
  Register #(.trigger("high")) register_4 (
    .D(multiplexer_4_out), .en(or_5_out), .Q(walls[31:24]), .clk(clock));  // open: clr
  or or_5 (or_5_out, initwalls, _3);
  D_Flip_Flop d_ff_2 (.Q(d_ff_2_q), .preset(of1), .reset(reset));  // open: clk, D, Qn, en
  D_Flip_Flop d_ff_3 (.D(of2), .Q(d_ff_3_q), .preset(of2), .reset(reset));  // open: clk, Qn, en
  D_Flip_Flop d_ff_4 (.D(or_1_out), .Q(d_ff_4_q), .preset(or_1_out), .reset(reset));  // open: clk, Qn, en
  Multiplexer multiplexer_5 (.in0(1'b0), .in1(1'b1), .out(reset), .sel(resreg));  // open: en
  Priority_Encoder #(.select(2)) priority_encoder_1 (
    .in0(d_ff_4_q), .in1(d_ff_2_q), .in2(d_ff_3_q), .out(ctr));  // open: in3, gs, en_out, en_in
  Demultiplexer #(.select(2)) demultiplexer_2 (
    .out0(clk1), .out1(clk2), .out2(clk3), .in(clock), .sel(ctr));  // open: out3, en
  \передача_данных  \u_передача_данных_1  (
    .data(walls), .slowenclock(clk2), .adress(8'h2b), .dataout(walldat), .adressout(walladr), .of(of2),
    .res(reset));
  // Probe on adress
  Comparator #(.mode("unsigned")) comparator_1 (.a(adress), .b(8'h33), .gt(comparator_1_gt));  // open: eq, lt
  Comparator #(.mode("unsigned")) comparator_2 (.a(adress), .b(8'h38), .lt(comparator_2_lt));  // open: gt, eq
  Comparator comparator_3 (.a(cdm_8_mark5_1_r3), .b({8{1'b1}}), .eq(resreg));  // open: gt, lt
  Comparator comparator_4 (.a(adress), .b({8{1'b0}}));  // open: gt, eq, lt
  Subtractor subtractor_1 (.a(adress), .b(8'h34), .out({subtractor_1_out, index}));  // open: bin, bout
  and and_1 (writenow, comparator_1_gt, comparator_2_lt);
  CdM_8_mark5 cdm_8_mark5_1 (
    .clock(clk3), .addr(adress), .mem_read(READwrite), .mem_cycle(cdm_8_mark5_1_mem_cycle),
    .data_inst(cdm_8_mark5_1_data_inst), .data_out(cdm_8_mark5_1_data_out),
    .data_in(controlled_buffer_2_out), .r3(cdm_8_mark5_1_r3), .IAck(IAck), .IRQ(IRQ), .vec(vec));  // open: r0, r1, r2, PC, SP, PS, reset
  Multiplexer #(.select(2), .width(8)) multiplexer_6 (
    .in0(bulldat), .in1(walldat), .in2(IOdat), .out(multiplexer_6_out), .sel(ctr));  // open: in3, en
  and and_2 (IOsel, adress[4], adress[5], adress[6], adress[7], decoder_1_out1);
  Decoder #(.disabled(0)) decoder_1 (
    .out0(decoder_1_out0), .out1(decoder_1_out1), .sel(cdm_8_mark5_1_data_inst), .en(cdm_8_mark5_1_mem_cycle));
  not not_1 (not_1_out, READwrite);
  assign IOdat = not_1_out ? cdm_8_mark5_1_data_out : 8'bz;  // Controlled_Buffer controlled_buffer_1
  assign controlled_buffer_2_out = READwrite ? IOdat : 8'bz;  // Controlled_Buffer controlled_buffer_2
  Register register_5 (.D(IOdat), .en(writenow), .Q(walls_t), .clk(clk3));  // open: clr
  // Probe on adress
  and and_3 (and_3_out, decoder_1_out1, ~IOsel);  // AND_Gate
  // Probe on multiplexer_7_out
  Multiplexer #(.select(2), .width(8)) multiplexer_7 (
    .in0(bulladr), .in1(walladr), .in2(adress), .out(multiplexer_7_out), .sel(ctr));  // open: in3, en
  Comparator comparator_5 (.a({subtractor_1_out, index}), .b({8{1'b0}}), .eq(_0));  // open: gt, lt
  Comparator comparator_6 (.a({subtractor_1_out, index}), .b(8'h1), .eq(_1));  // open: gt, lt
  Comparator comparator_7 (.a({subtractor_1_out, index}), .b(8'h2), .eq(_2));  // open: gt, lt
  Comparator comparator_8 (.a({subtractor_1_out, index}), .b(8'h3), .eq(_3));  // open: gt, lt
  Multiplexer multiplexer_8 (.in0(1'b0), .in1(READwrite), .out(multiplexer_8_out), .sel(of2));  // open: en
  or or_6 (or_6_out, and_3_out, ~of2);  // OR_Gate
  not not_2 (not_2_out, clock);
  // Probe on IOdat
  RAM #(.bus("separate")) ram_1 (
    .addr(multiplexer_7_out), .din(multiplexer_6_out), .data(IOdat), .sel(or_6_out), .clk(not_2_out),
    .ld(multiplexer_8_out));  // open: str, clr
  ROM rom_1 (.addr(adress), .data(IOdat), .sel(decoder_1_out0));

  // Other names for the same wires on the sheet: IOaddr[3:0] = adress[3:0]; clk = clock

  // Notes on the sheet:
  //   contents of rom_1 (hex, n*v repeats v):
  //   d0 2c d1 30 d2 0 c1 19 b5 5 e0 19 c0 18 b0 1 25 41 d0 34 18 a1 c4 ee 21 c0 18 b0 d1 34 19 a4 c4 c5
  //   d0 2d d1 31 c1 19 b5 5 e0 39 c0 18 b0 1 25 41 d0 35 18 a1 c4 ee 41 c0 18 b0 d1 35 19 a4 c4 c5 d0 2e
  //   d1 32 c1 19 b5 5 e0 59 c0 18 b0 1 25 41 d0 36 18 a1 c4 ee 61 c0 18 b0 d1 36 19 a4 c4 c5 d0 2f d1 33
  //   c1 19 b5 5 e0 79 c0 18 b0 1 25 41 d0 37 18 a1 c4 ee 81 c0 18 b0 d1 37 19 a4 c4 c5 d4
endmodule

module \попадание  (
  input  [31:0] A,
  input  [31:0] B,
  output [31:0] OUT
);

  wire [31:0] xnor_1_out;

  assign xnor_1_out = ~(A ^ B);  // XNOR_Gate xnor_1, 32 bits wide
  and and_1 (OUT[0], xnor_1_out[0], B[0]);
  and and_2 (OUT[1], xnor_1_out[1], B[1]);
  and and_3 (OUT[2], xnor_1_out[2], B[2]);
  and and_4 (OUT[3], xnor_1_out[3], B[3]);
  and and_5 (OUT[4], xnor_1_out[4], B[4]);
  and and_6 (OUT[5], xnor_1_out[5], B[5]);
  and and_7 (OUT[6], xnor_1_out[6], B[6]);
  and and_8 (OUT[7], xnor_1_out[7], B[7]);
  and and_9 (OUT[8], xnor_1_out[8], B[8]);
  and and_10 (OUT[9], xnor_1_out[9], B[9]);
  and and_11 (OUT[10], xnor_1_out[10], B[10]);
  and and_12 (OUT[11], xnor_1_out[11], B[11]);
  and and_13 (OUT[12], xnor_1_out[12], B[12]);
  and and_14 (OUT[13], xnor_1_out[13], B[13]);
  and and_15 (OUT[14], xnor_1_out[14], B[14]);
  and and_16 (OUT[15], xnor_1_out[15], B[15]);
  and and_17 (OUT[16], xnor_1_out[16], B[16]);
  and and_18 (OUT[17], xnor_1_out[17], B[17]);
  and and_19 (OUT[18], xnor_1_out[18], B[18]);
  and and_20 (OUT[19], xnor_1_out[19], B[19]);
  and and_21 (OUT[20], xnor_1_out[20], B[20]);
  and and_22 (OUT[21], xnor_1_out[21], B[21]);
  and and_23 (OUT[22], xnor_1_out[22], B[22]);
  and and_24 (OUT[23], xnor_1_out[23], B[23]);
  and and_25 (OUT[24], xnor_1_out[24], B[24]);
  and and_26 (OUT[25], xnor_1_out[25], B[25]);
  and and_27 (OUT[26], xnor_1_out[26], B[26]);
  and and_28 (OUT[27], xnor_1_out[27], B[27]);
  and and_29 (OUT[28], xnor_1_out[28], B[28]);
  and and_30 (OUT[29], xnor_1_out[29], B[29]);
  and and_31 (OUT[30], xnor_1_out[30], B[30]);
  and and_32 (OUT[31], xnor_1_out[31], B[31]);

  // Other names for the same wires on the sheet: _0 = OUT[0]; _1 = OUT[1]; _2 = OUT[2]; _3 = OUT[3]; _4 = OUT[4];
  //   _5 = OUT[5]; _6 = OUT[6]; _7 = OUT[7]; _8 = OUT[8]; _9 = OUT[9]; _10 = OUT[10]; _11 = OUT[11]; _12 = OUT[12];
  //   _13 = OUT[13]; _14 = OUT[14]; _15 = OUT[15]; _16 = OUT[16]; _17 = OUT[17]; _18 = OUT[18]; _19 = OUT[19];
  //   _20 = OUT[20]; _21 = OUT[21]; _22 = OUT[22]; _23 = OUT[23]; _24 = OUT[24]; _25 = OUT[25]; _26 = OUT[26];
  //   _27 = OUT[27]; _28 = OUT[28]; _29 = OUT[29]; _30 = OUT[30]; _31 = OUT[31]
endmodule

module \стрельба  (
  input  [4:0] coord,
  input  fire,
  input  clk,
  output [31:0] out_4,
  output [31:0] out_5,
  output [31:0] out_6,
  output [31:0] out_7,
  output [31:0] out_8,
  output [31:0] out_9,
  output [31:0] out_10,
  output [31:0] out_11,
  output [31:0] out_12,
  output [31:0] out_13,
  output [31:0] out_14,
  output [31:0] out_15,
  output [31:0] out_16,
  output [31:0] out_17,
  output [31:0] out_18,
  output [31:0] out_19,
  output [31:0] out_20,
  output [31:0] out_21,
  output [31:0] out_22,
  output [31:0] out_23,
  output [31:0] out_24,
  output [31:0] out_25,
  output [31:0] out_26,
  output [31:0] out_27,
  output [31:0] out_28,
  output [31:0] out_29,
  output [31:0] out_30,
  output [31:0] out_31,
  output [31:0] out_32,
  output [31:0] out_33
);

  wire A0, and_1_out, and_2_out, and_3_out, and_4_out, and_5_out, and_6_out, and_7_out, and_8_out,
       and_10_out, and_11_out, and_12_out, B1, B2, B3, cdm_8_mark5_1_data_inst, cdm_8_mark5_1_mem_cycle,
       cdm_8_mark5_1_mem_read, comparator_1_gt, comparator_2_eq, comparator_3_eq, comparator_4_eq,
       comparator_5_eq, comparator_6_eq, comparator_7_eq, comparator_8_eq, controlled_buffer_3_out,
       decoder_1_out0, decoder_1_out1, fire_t, got1_2_out_2, got1_3_out_2, got1_4_out_2, not_1_out,
       not_2_out, not_3_out, or_1_out, or_2_out, or_3_out, or_4_out, or_5_out, or_6_out, oradd8_1_out,
       oradd8_2_out, oradd8_3_out, oradd32_1_out, OUT, pull_resistor_1_node, started;
  wire [1:0] priority_encoder_1_out;
  wire [4:0] register_1_q, subtractor_1_out;
  wire [7:0] addr, buffer_1_out, buffer_2_out, cdm_8_mark5_1_data_out, cdm_8_mark5_1_ps, cdm_8_mark5_1_r0,
       cdm_8_mark5_1_r1, cdm_8_mark5_1_r2, cdm_8_mark5_1_sp, controlled_buffer_4_out,
       controlled_buffer_5_out, controlled_buffer_7_out, controlled_buffer_8_out, controlled_buffer_9_out,
       controlled_buffer_10_out, demultiplexer_4_out0, demultiplexer_4_out1, demultiplexer_4_out2,
       demultiplexer_4_out3, io_data, PC, r3, sub_1_p3;
  wire [31:0] demultiplexer_1_out0, demultiplexer_1_out1, demultiplexer_1_out2, demultiplexer_1_out3,
       demultiplexer_1_out4, demultiplexer_1_out5, demultiplexer_1_out6, demultiplexer_1_out7,
       demultiplexer_1_out8, demultiplexer_1_out9, demultiplexer_1_out10, demultiplexer_1_out11,
       demultiplexer_1_out12, demultiplexer_1_out13, demultiplexer_1_out14, demultiplexer_1_out15,
       demultiplexer_1_out16, demultiplexer_1_out17, demultiplexer_1_out18, demultiplexer_1_out19,
       demultiplexer_1_out20, demultiplexer_1_out21, demultiplexer_1_out22, demultiplexer_1_out23,
       demultiplexer_1_out24, demultiplexer_1_out25, demultiplexer_1_out26, demultiplexer_1_out27,
       demultiplexer_1_out28, demultiplexer_1_out29, demultiplexer_1_out30, demultiplexer_1_out31, st;

  Comparator comparator_1 (.a(PC), .b(8'h18), .gt(comparator_1_gt));  // open: eq, lt
  oradd32 oradd32_1 (.in(st), .out(oradd32_1_out));
  and and_1 (and_1_out, ~oradd32_1_out, comparator_1_gt);  // AND_Gate
  or or_1 (or_1_out, ~started, and_1_out);  // OR_Gate
  Pull_Resistor pull_resistor_1 (.node(pull_resistor_1_node));
  assign pull_resistor_1_node = or_1_out ? fire : 1'bz;  // Controlled_Buffer controlled_buffer_1
  got1 got1_1 (.in_1(pull_resistor_1_node), .out_2(fire_t));
  Subtractor #(.width(5)) subtractor_1 (.a({5{1'b1}}), .b(coord), .out(subtractor_1_out));  // open: bin, bout
  // Probe on subtractor_1_out
  Demultiplexer #(.select(5), .width(32)) demultiplexer_1 (
    .out0(demultiplexer_1_out0), .out1(demultiplexer_1_out1), .out2(demultiplexer_1_out2),
    .out3(demultiplexer_1_out3), .out4(demultiplexer_1_out4), .out5(demultiplexer_1_out5),
    .out6(demultiplexer_1_out6), .out7(demultiplexer_1_out7), .out8(demultiplexer_1_out8),
    .out9(demultiplexer_1_out9), .out10(demultiplexer_1_out10), .out11(demultiplexer_1_out11),
    .out12(demultiplexer_1_out12), .out13(demultiplexer_1_out13), .out14(demultiplexer_1_out14),
    .out15(demultiplexer_1_out15), .out16(demultiplexer_1_out16), .out17(demultiplexer_1_out17),
    .out18(demultiplexer_1_out18), .out19(demultiplexer_1_out19), .out20(demultiplexer_1_out20),
    .out21(demultiplexer_1_out21), .out22(demultiplexer_1_out22), .out23(demultiplexer_1_out23),
    .out24(demultiplexer_1_out24), .out25(demultiplexer_1_out25), .out26(demultiplexer_1_out26),
    .out27(demultiplexer_1_out27), .out28(demultiplexer_1_out28), .out29(demultiplexer_1_out29),
    .out30(demultiplexer_1_out30), .out31(demultiplexer_1_out31), .in(st), .sel(register_1_q));  // open: en
  Register #(.width(5)) register_1 (.D(subtractor_1_out), .en(fire_t), .Q(register_1_q), .clk(fire_t));  // open: clr
  transpon transpon_1 (
    .in_1(demultiplexer_1_out0), .in_2(demultiplexer_1_out1), .in_3(demultiplexer_1_out2),
    .in_4(demultiplexer_1_out3), .in_5(demultiplexer_1_out4), .in_6(demultiplexer_1_out5),
    .in_7(demultiplexer_1_out6), .in_8(demultiplexer_1_out7), .in_9(demultiplexer_1_out8),
    .in_10(demultiplexer_1_out9), .in_11(demultiplexer_1_out10), .in_12(demultiplexer_1_out11),
    .in_13(demultiplexer_1_out12), .in_14(demultiplexer_1_out13), .in_15(demultiplexer_1_out14),
    .in_16(demultiplexer_1_out15), .in_17(demultiplexer_1_out16), .in_18(demultiplexer_1_out17),
    .in_19(demultiplexer_1_out18), .in_20(demultiplexer_1_out19), .in_21(demultiplexer_1_out20),
    .in_22(demultiplexer_1_out21), .in_23(demultiplexer_1_out22), .in_24(demultiplexer_1_out23),
    .in_25(demultiplexer_1_out24), .in_26(demultiplexer_1_out25), .in_27(demultiplexer_1_out26),
    .in_28(demultiplexer_1_out27), .in_29(demultiplexer_1_out28), .in_30(demultiplexer_1_out29),
    .in_31(demultiplexer_1_out30), .in_32(demultiplexer_1_out31), ._2(out_4), ._3(out_5), ._4(out_6),
    ._5(out_7), ._6(out_8), ._7(out_9), ._8(out_10), ._9(out_11), ._10(out_12), ._11(out_13), ._12(out_14),
    ._13(out_15), ._14(out_16), ._15(out_17), ._16(out_18), ._17(out_19), ._18(out_20), ._19(out_21),
    ._20(out_22), ._21(out_23), ._22(out_24), ._23(out_25), ._24(out_26), ._25(out_27), ._26(out_28),
    ._27(out_29), ._28(out_30), ._29(out_31), ._30(out_32), ._31(out_33));  // open: _0, _1
  Comparator comparator_2 (.a(PC), .b(8'h5), .eq(comparator_2_eq));  // open: gt, lt
  Comparator comparator_3 (.a(PC), .b(8'hd), .eq(comparator_3_eq));  // open: gt, lt
  Comparator comparator_4 (.a(PC), .b(8'h12), .eq(comparator_4_eq));  // open: gt, lt
  Comparator comparator_5 (.a(addr), .b(8'h60), .eq(comparator_5_eq));  // open: gt, lt
  Comparator comparator_6 (.a(addr), .b(8'h61), .eq(comparator_6_eq));  // open: gt, lt
  Comparator comparator_7 (.a(addr), .b(8'h62), .eq(comparator_7_eq));  // open: gt, lt
  Comparator comparator_8 (.a(addr), .b(8'h63), .eq(comparator_8_eq));  // open: gt, lt
  or or_2 (or_2_out, comparator_2_eq, comparator_3_eq, comparator_4_eq);
  and and_2 (and_2_out, comparator_5_eq, or_2_out);
  and and_3 (and_3_out, comparator_6_eq, or_2_out);
  and and_4 (and_4_out, comparator_7_eq, or_2_out);
  and and_5 (and_5_out, comparator_8_eq, or_2_out);
  assign A0 = fire_t ? fire_t : 1'bz;  // Controlled_Buffer controlled_buffer_2
  D_Flip_Flop d_ff_1 (.Q(started), .preset(fire_t));  // open: clk, D, Qn, en, reset
  Demultiplexer #(.select(2)) demultiplexer_2 (
    .out1(B1), .out2(B2), .out3(B3), .in(1'b1), .sel(sub_1_p3[1:0]), .en(and_6_out));  // open: out0
  and and_6 (and_6_out, comparator_4_eq, OUT);
  // sub sub_1: pin names not known; wires that end beside it: 8'h5, r3, sub_1_p3, sub_1_p3[1:0]
  and and_7 (and_7_out, addr[4], addr[5], addr[6], addr[7], decoder_1_out1);
  // Probe on r3
  // Probe on cdm_8_mark5_1_r2
  // Probe on cdm_8_mark5_1_r1
  // Probe on cdm_8_mark5_1_r0
  assign controlled_buffer_3_out = started ? clk : 1'bz;  // Controlled_Buffer controlled_buffer_3
  Priority_Encoder #(.select(2)) priority_encoder_1 (
    .in0(and_2_out), .in1(and_3_out), .in2(and_4_out), .in3(and_5_out), .out(priority_encoder_1_out));  // open: gs, en_out, en_in
  or or_3 (or_3_out, and_5_out, and_4_out, and_3_out, and_2_out);
  \попадание  \u_попадание_1  ();  // open: OUT, A, B
  and and_8 (and_8_out, decoder_1_out1, ~and_7_out);  // AND_Gate
  // Probe on PC
  // Probe on cdm_8_mark5_1_ps
  // Probe on cdm_8_mark5_1_sp
  CdM_8_mark5 cdm_8_mark5_1 (
    .clock(controlled_buffer_3_out), .addr(addr), .mem_read(cdm_8_mark5_1_mem_read),
    .mem_cycle(cdm_8_mark5_1_mem_cycle), .data_inst(cdm_8_mark5_1_data_inst),
    .data_out(cdm_8_mark5_1_data_out), .data_in(controlled_buffer_5_out), .r0(cdm_8_mark5_1_r0),
    .r1(cdm_8_mark5_1_r1), .r2(cdm_8_mark5_1_r2), .r3(r3), .PC(PC), .SP(cdm_8_mark5_1_sp),
    .PS(cdm_8_mark5_1_ps), .reset(fire_t));  // open: IAck, IRQ, vec
  and and_9 (OUT, or_2_out, or_3_out);
  Demultiplexer #(.select(2)) demultiplexer_3 (
    .out0(A0), .out1(A0), .out2(A0), .out3(A0), .in(1'b1), .sel(priority_encoder_1_out), .en(OUT));
  Decoder #(.disabled(0)) decoder_1 (
    .out0(decoder_1_out0), .out1(decoder_1_out1), .sel(cdm_8_mark5_1_data_inst), .en(cdm_8_mark5_1_mem_cycle));
  not not_1 (not_1_out, cdm_8_mark5_1_mem_read);
  assign controlled_buffer_4_out = not_1_out ? cdm_8_mark5_1_data_out : 8'bz;  // Controlled_Buffer controlled_buffer_4
  assign controlled_buffer_5_out = cdm_8_mark5_1_mem_read ? controlled_buffer_4_out : 8'bz;  // Controlled_Buffer controlled_buffer_5
  assign io_data = OUT ? controlled_buffer_4_out : 8'bz;  // Controlled_Buffer controlled_buffer_6
  Demultiplexer #(.select(2), .width(8)) demultiplexer_4 (
    .out0(demultiplexer_4_out0), .out1(demultiplexer_4_out1), .out2(demultiplexer_4_out2),
    .out3(demultiplexer_4_out3), .in(io_data), .sel(priority_encoder_1_out), .en(OUT));
  // Probe on addr
  // Probe on controlled_buffer_4_out
  RAM #(.bus("separate")) ram_1 (
    .addr(addr), .data(controlled_buffer_4_out), .sel(and_8_out), .clk(not_2_out),
    .ld(cdm_8_mark5_1_mem_read), .clr(fire_t));  // open: din, str
  not not_2 (not_2_out, clk);
  ROM rom_1 (.addr(addr), .data(controlled_buffer_4_out), .sel(decoder_1_out0));
  // Probe on controlled_buffer_4_out
  oradd8 oradd8_1 (.in(st[7:0]), .out(oradd8_1_out));
  and and_10 (and_10_out, ~oradd8_1_out, B1);  // AND_Gate
  not not_3 (not_3_out, and_10_out);
  assign controlled_buffer_7_out = not_3_out ? demultiplexer_4_out1 : 8'bz;  // Controlled_Buffer controlled_buffer_7
  oradd8 oradd8_2 (.in(st[15:8]), .out(oradd8_2_out));
  assign buffer_1_out = demultiplexer_4_out2;  // Buffer buffer_1, 8 bits wide
  Pull_Resistor pull_resistor_2 (.node(B2));
  Pull_Resistor pull_resistor_3 (.node(A0));
  oradd8 oradd8_3 (.in(st[23:16]), .out(oradd8_3_out));
  assign buffer_2_out = demultiplexer_4_out3;  // Buffer buffer_2, 8 bits wide
  Pull_Resistor pull_resistor_4 (.node(B3));
  Pull_Resistor pull_resistor_5 (.node(A0));
  // Probe on controlled_buffer_4_out
  Pull_Resistor pull_resistor_6 (.node(A0));
  assign controlled_buffer_8_out = and_10_out ? 8'h1 : 8'bz;  // Controlled_Buffer controlled_buffer_8
  Pull_Resistor pull_resistor_7 (.node(B1));
  got1 got1_2 (.in_1(B1), .out_2(got1_2_out_2));
  Pull_Resistor pull_resistor_8 (.node(A0));
  and and_11 (and_11_out, ~oradd8_2_out, B2);  // AND_Gate
  assign controlled_buffer_9_out = and_11_out ? 8'h1 : 8'bz;  // Controlled_Buffer controlled_buffer_9
  got1 got1_3 (.in_1(B2), .out_2(got1_3_out_2));
  and and_12 (and_12_out, ~oradd8_3_out, B3);  // AND_Gate
  assign controlled_buffer_10_out = and_12_out ? 8'h1 : 8'bz;  // Controlled_Buffer controlled_buffer_10
  got1 got1_4 (.in_1(B3), .out_2(got1_4_out_2));
  Register register_2 (.D(demultiplexer_4_out0), .en(A0), .Q(st[7:0]), .clk(clk));  // open: clr
  got1 got1_5 (.in_1(controlled_buffer_8_out[0]), .out_2(controlled_buffer_7_out[0]));
  or or_4 (or_4_out, got1_2_out_2, A0);
  got1 got1_6 (.in_1(controlled_buffer_9_out[0]), .out_2(buffer_1_out[0]));
  or or_5 (or_5_out, got1_3_out_2, A0);
  got1 got1_7 (.in_1(controlled_buffer_10_out[0]), .out_2(buffer_2_out[0]));
  or or_6 (or_6_out, got1_4_out_2, A0);
  Pull_Resistor pull_resistor_9 (.node(controlled_buffer_7_out[7:1]));
  Register register_3 (.D(controlled_buffer_7_out), .en(or_4_out), .Q(st[15:8]), .clk(clk));  // open: clr
  Pull_Resistor pull_resistor_10 (.node(buffer_1_out[7:1]));
  Register register_4 (.D(buffer_1_out), .en(or_5_out), .Q(st[23:16]), .clk(clk));  // open: clr
  Pull_Resistor pull_resistor_11 (.node(buffer_2_out[7:1]));
  Register register_5 (.D(buffer_2_out), .en(or_6_out), .Q(st[31:24]), .clk(clk));  // open: clr

  // Other names for the same wires on the sheet: _2[31:0] = out_4; _3[31:0] = out_5; _4[31:0] = out_6;
  //   _5[31:0] = out_7; _6[31:0] = out_8; _7[31:0] = out_9; _8[31:0] = out_10; _9[31:0] = out_11; _10[31:0] = out_12;
  //   _11[31:0] = out_13; _12[31:0] = out_14; _13[31:0] = out_15; _14[31:0] = out_16; _15[31:0] = out_17;
  //   _16[31:0] = out_18; _17[31:0] = out_19; _18[31:0] = out_20; _19[31:0] = out_21; _20[31:0] = out_22;
  //   _21[31:0] = out_23; _22[31:0] = out_24; _23[31:0] = out_25; _24[31:0] = out_26; _25[31:0] = out_27;
  //   _26[31:0] = out_28; _27[31:0] = out_29; _28[31:0] = out_30; _29[31:0] = out_31; _30[31:0] = out_32;
  //   _31[31:0] = out_33; A1 = A0; A2 = A0; A3 = A0; IOaddr[3:0] = addr[3:0]

  // Notes on the sheet:
  //   Столбец из пуль
  //   Адреса массива
  //   запись (сравнение с PC, когда st)
  //   устранение мерцания
  //   contents of rom_1 (hex, n*v repeats v):
  //   d0 3 d1 60 a4 d3 4 f e0 18 d0 2 a4 0 e0 14 94 a4 ee d 8d 8b ee 7 d4
  //   buffer_1 drives only 1 and floats otherwise
  //   buffer_2 drives only 1 and floats otherwise
  //   устранение мерцания. Доведения состояния "везде нули" до минимума
endmodule

// 0x7
module \передача_данных  (
  input  [31:0] data,
  input  slowenclock,
  input  res,
  input  [7:0] adress,
  output [7:0] dataout,
  output [7:0] adressout,
  output of
);

  wire [1:0] counter_1_q;
  wire [2:2] counter_1_q_2;
  wire [7:0] bit_extender_1_out;

  Multiplexer #(.select(2), .width(8)) multiplexer_1 (
    .in0(data[7:0]), .in1(data[15:8]), .in2(data[23:16]), .in3(data[31:24]), .out(dataout), .sel(counter_1_q));  // open: en
  Counter #(.width(3), .max('h5)) counter_1 (
    .Q({counter_1_q_2[2], counter_1_q}), .carry(of), .clk(slowenclock), .clr(res));  // open: load, D, count
  assign bit_extender_1_out = {{5{1'b0}}, {counter_1_q_2[2], counter_1_q}};  // Bit_Extender bit_extender_1
  Adder adder_1 (.a(bit_extender_1_out), .b(adress), .out(adressout));  // open: cin, cout
endmodule

module menu (
  input  [4:0] in,
  output [31:0] out
);

  wire decoder_1_out0, decoder_1_out1, decoder_1_out2, decoder_1_out3, decoder_1_out4, decoder_1_out5,
       decoder_1_out6, decoder_1_out7, decoder_1_out8, decoder_1_out9, decoder_1_out10, decoder_1_out11,
       decoder_1_out12, decoder_1_out13, decoder_1_out14, decoder_1_out15, decoder_1_out16, decoder_1_out17,
       decoder_1_out18, decoder_1_out19, decoder_1_out20, decoder_1_out21, decoder_1_out22, decoder_1_out23,
       decoder_1_out24, decoder_1_out25, decoder_1_out26, decoder_1_out27, decoder_1_out28, decoder_1_out29,
       decoder_1_out30, decoder_1_out31;
  wire [31:0] pull_resistor_1_node, pull_resistor_2_node, pull_resistor_3_node;

  Pull_Resistor pull_resistor_1 (.node(pull_resistor_1_node));
  Pull_Resistor pull_resistor_2 (.node(pull_resistor_2_node));
  Pull_Resistor pull_resistor_3 (.node(pull_resistor_3_node));
  Decoder #(.select(5), .disabled(0), .enable("false")) decoder_1 (
    .out0(decoder_1_out0), .out1(decoder_1_out1), .out2(decoder_1_out2), .out3(decoder_1_out3),
    .out4(decoder_1_out4), .out5(decoder_1_out5), .out6(decoder_1_out6), .out7(decoder_1_out7),
    .out8(decoder_1_out8), .out9(decoder_1_out9), .out10(decoder_1_out10), .out11(decoder_1_out11),
    .out12(decoder_1_out12), .out13(decoder_1_out13), .out14(decoder_1_out14), .out15(decoder_1_out15),
    .out16(decoder_1_out16), .out17(decoder_1_out17), .out18(decoder_1_out18), .out19(decoder_1_out19),
    .out20(decoder_1_out20), .out21(decoder_1_out21), .out22(decoder_1_out22), .out23(decoder_1_out23),
    .out24(decoder_1_out24), .out25(decoder_1_out25), .out26(decoder_1_out26), .out27(decoder_1_out27),
    .out28(decoder_1_out28), .out29(decoder_1_out29), .out30(decoder_1_out30), .out31(decoder_1_out31),
    .sel(in));
  assign out = decoder_1_out28 ? pull_resistor_3_node : 32'bz;  // Controlled_Buffer controlled_buffer_1
  assign out = decoder_1_out29 ? pull_resistor_3_node : 32'bz;  // Controlled_Buffer controlled_buffer_2
  assign out = decoder_1_out30 ? pull_resistor_3_node : 32'bz;  // Controlled_Buffer controlled_buffer_3
  assign out = decoder_1_out31 ? pull_resistor_3_node : 32'bz;  // Controlled_Buffer controlled_buffer_4
  assign out = decoder_1_out25 ? 32'h45141040 : 32'bz;  // Controlled_Buffer controlled_buffer_5
  assign out = decoder_1_out26 ? 32'h45141040 : 32'bz;  // Controlled_Buffer controlled_buffer_6
  assign out = decoder_1_out27 ? 32'h7df7df7c : 32'bz;  // Controlled_Buffer controlled_buffer_7
  assign out = decoder_1_out22 ? 32'h41840104 : 32'bz;  // Controlled_Buffer controlled_buffer_8
  assign out = decoder_1_out23 ? 32'h7df7df7c : 32'bz;  // Controlled_Buffer controlled_buffer_9
  assign out = decoder_1_out24 ? 32'h45141040 : 32'bz;  // Controlled_Buffer controlled_buffer_10
  assign out = decoder_1_out19 ? pull_resistor_2_node : 32'bz;  // Controlled_Buffer controlled_buffer_11
  assign out = decoder_1_out20 ? 32'h4117df7c : 32'bz;  // Controlled_Buffer controlled_buffer_12
  assign out = decoder_1_out21 ? 32'h41240104 : 32'bz;  // Controlled_Buffer controlled_buffer_13
  assign out = decoder_1_out15 ? pull_resistor_2_node : 32'bz;  // Controlled_Buffer controlled_buffer_14
  assign out = decoder_1_out16 ? pull_resistor_2_node : 32'bz;  // Controlled_Buffer controlled_buffer_15
  assign out = decoder_1_out17 ? pull_resistor_2_node : 32'bz;  // Controlled_Buffer controlled_buffer_16
  assign out = decoder_1_out18 ? pull_resistor_2_node : 32'bz;  // Controlled_Buffer controlled_buffer_17
  assign out = decoder_1_out12 ? 32'h7df7dfbe : 32'bz;  // Controlled_Buffer controlled_buffer_18
  assign out = decoder_1_out13 ? pull_resistor_2_node : 32'bz;  // Controlled_Buffer controlled_buffer_19
  assign out = decoder_1_out14 ? pull_resistor_2_node : 32'bz;  // Controlled_Buffer controlled_buffer_20
  assign out = decoder_1_out9 ? 32'h40445088 : 32'bz;  // Controlled_Buffer controlled_buffer_21
  assign out = decoder_1_out10 ? 32'h40445088 : 32'bz;  // Controlled_Buffer controlled_buffer_22
  assign out = decoder_1_out11 ? 32'h40445088 : 32'bz;  // Controlled_Buffer controlled_buffer_23
  assign out = decoder_1_out5 ? 32'h7c445108 : 32'bz;  // Controlled_Buffer controlled_buffer_24
  assign out = decoder_1_out6 ? 32'h4445208 : 32'bz;  // Controlled_Buffer controlled_buffer_25
  assign out = decoder_1_out7 ? 32'h4445808 : 32'bz;  // Controlled_Buffer controlled_buffer_26
  assign out = decoder_1_out8 ? 32'h7c47df88 : 32'bz;  // Controlled_Buffer controlled_buffer_27
  assign out = decoder_1_out1 ? pull_resistor_1_node : 32'bz;  // Controlled_Buffer controlled_buffer_28
  assign out = decoder_1_out2 ? pull_resistor_1_node : 32'bz;  // Controlled_Buffer controlled_buffer_29
  assign out = decoder_1_out3 ? pull_resistor_1_node : 32'bz;  // Controlled_Buffer controlled_buffer_30
  assign out = decoder_1_out4 ? pull_resistor_1_node : 32'bz;  // Controlled_Buffer controlled_buffer_31
  assign out = decoder_1_out0 ? pull_resistor_1_node : 32'bz;  // Controlled_Buffer controlled_buffer_32
endmodule

module circ (
  input  on,
  input  isgameover,
  input  start,
  input  [4:0] counter,
  input  [31:0] game,
  input  endgame,
  output [31:0] out_7
);

  wire and_1_out, and_2_out, not_1_out;
  wire [31:0] gameover_1_out, menu_1_out;

  not not_1 (not_1_out, on);
  and and_1 (and_1_out, on, ~start);  // AND_Gate
  menu menu_1 (.in(counter), .out(menu_1_out));
  and and_2 (and_2_out, on, ~endgame, start);  // AND_Gate
  assign out_7 = not_1_out ? {32{1'b0}} : 32'bz;  // Controlled_Buffer controlled_buffer_1
  assign out_7 = and_1_out ? menu_1_out : 32'bz;  // Controlled_Buffer controlled_buffer_2
  assign out_7 = and_2_out ? game : 32'bz;  // Controlled_Buffer controlled_buffer_3
  gameover gameover_1 (.in(counter), .isGameOver(isgameover), .out(gameover_1_out));
  assign out_7 = endgame ? gameover_1_out : 32'bz;  // Controlled_Buffer controlled_buffer_4
endmodule

module menumega (
  input  gameover,
  input  endgame,
  input  on,
  input  [4:0] beg,
  input  start,
  input  [31:0] in_6,
  input  [31:0] in_7,
  input  [31:0] in_8,
  input  [31:0] in_9,
  input  [31:0] in_10,
  input  [31:0] in_11,
  input  [31:0] in_12,
  input  [31:0] in_13,
  output [31:0] out_14,
  output [31:0] out_15,
  output [31:0] out_16,
  output [31:0] out_17,
  output [31:0] out_18,
  output [31:0] out_19,
  output [31:0] out_20,
  output [31:0] out_21,
  output [4:0] \end 
);

  wire [4:0] inc5_1_r, inc5_2_r, inc5_3_r, inc5_4_r, inc5_5_r, inc5_7_r;

  circ circ_1 (
    .on(on), .start(start), .counter(beg), .game(in_6), .out_7(out_14), .isgameover(gameover),
    .endgame(endgame));
  circ circ_2 (
    .on(on), .start(start), .counter(inc5_1_r), .game(in_7), .out_7(out_15), .isgameover(gameover),
    .endgame(endgame));
  circ circ_3 (
    .on(on), .start(start), .counter(inc5_2_r), .game(in_10), .out_7(out_18), .isgameover(gameover),
    .endgame(endgame));
  inc5 inc5_1 (.X(inc5_2_r), .R(inc5_1_r));  // open: Cout
  inc5 inc5_2 (.X(beg), .R(inc5_2_r));  // open: Cout
  circ circ_4 (
    .on(on), .start(start), .counter(inc5_3_r), .game(in_11), .out_7(out_19), .isgameover(gameover),
    .endgame(endgame));
  inc5 inc5_3 (.X(inc5_1_r), .R(inc5_3_r));  // open: Cout
  inc5 inc5_4 (.X(inc5_3_r), .R(inc5_4_r));  // open: Cout
  circ circ_5 (
    .on(on), .start(start), .counter(inc5_5_r), .game(in_12), .out_7(out_20), .isgameover(gameover),
    .endgame(endgame));
  circ circ_6 (
    .on(on), .start(start), .counter(inc5_4_r), .game(in_8), .out_7(out_16), .isgameover(gameover),
    .endgame(endgame));
  inc5 inc5_5 (.X(inc5_4_r), .R(inc5_5_r));  // open: Cout
  circ circ_7 (
    .on(on), .start(start), .counter(inc5_7_r), .game(in_9), .out_7(out_17), .isgameover(gameover),
    .endgame(endgame));
  inc5 inc5_6 (.X(inc5_7_r), .R(\end ));  // open: Cout
  inc5 inc5_7 (.X(inc5_5_r), .R(inc5_7_r));  // open: Cout
  circ circ_8 (
    .on(on), .start(start), .counter(\end ), .game(in_13), .out_7(out_21), .isgameover(gameover),
    .endgame(endgame));
endmodule

module pentamenu (
  input  start,
  input  on,
  input  endGame,
  input  gameOver,
  input  [6:0] control,
  input  _8,
  input  _7,
  input  _6,
  input  _5,
  input  _4,
  input  _3,
  input  _2,
  input  _1,
  output [31:0] out_14,
  output [31:0] out_15,
  output [31:0] out_16,
  output [31:0] out_17,
  output [31:0] out_18,
  output [31:0] out_19,
  output [31:0] out_20,
  output [31:0] out_21,
  output [31:0] out_22,
  output [31:0] out_23,
  output [31:0] out_24,
  output [31:0] out_25,
  output [31:0] out_26,
  output [31:0] out_27,
  output [31:0] out_28,
  output [31:0] out_29,
  output [31:0] out_30,
  output [31:0] out_31,
  output [31:0] out_32,
  output [31:0] out_33,
  output [31:0] out_34,
  output [31:0] out_35,
  output [31:0] out_36,
  output [31:0] out_37,
  output [31:0] out_38,
  output [31:0] out_39,
  output [31:0] out_40,
  output [31:0] out_41,
  output [31:0] out_42,
  output [31:0] out_43,
  output [31:0] out_44,
  output [31:0] out_45
);

  wire on_t;
  wire [4:0] menumega_1_end, menumega_2_end, menumega_3_end;
  wire [31:0] main_1_out_3, main_1_out_4, main_1_out_5, main_1_out_6, main_1_out_7, main_1_out_8,
       main_1_out_9, main_1_out_10, main_1_out_11, main_1_out_12, main_1_out_13, main_1_out_14,
       main_1_out_15, main_1_out_16, main_1_out_17, main_1_out_18, main_1_out_19, main_1_out_20,
       main_1_out_21, main_1_out_22, main_1_out_23, main_1_out_24, main_1_out_25, main_1_out_26,
       main_1_out_27, main_1_out_28, main_1_out_29, main_1_out_30, main_1_out_31, main_1_out_32,
       main_1_out_33, main_1_out_34;

  Counter #(.width(1), .max('h1)) counter_1 (.count(on), .Q(on_t), .clk(on));  // open: load, D, carry, clr
  main main_1 (
    .out_3(main_1_out_3), .out_4(main_1_out_4), .out_5(main_1_out_5), .out_6(main_1_out_6),
    .out_7(main_1_out_7), .out_8(main_1_out_8), .out_9(main_1_out_9), .out_10(main_1_out_10),
    .out_11(main_1_out_11), .out_12(main_1_out_12), .out_13(main_1_out_13), .out_14(main_1_out_14),
    .out_15(main_1_out_15), .out_16(main_1_out_16), .out_17(main_1_out_17), .out_18(main_1_out_18),
    .out_19(main_1_out_19), .out_20(main_1_out_20), .out_21(main_1_out_21), .out_22(main_1_out_22),
    .out_23(main_1_out_23), .out_24(main_1_out_24), .out_25(main_1_out_25), .out_26(main_1_out_26),
    .out_27(main_1_out_27), .out_28(main_1_out_28), .out_29(main_1_out_29), .out_30(main_1_out_30),
    .out_31(main_1_out_31), .out_32(main_1_out_32), .out_33(main_1_out_33), .out_34(main_1_out_34),
    .initgame(start), .moving(control));
  menumega menumega_1 (
    .beg({5{1'b0}}), .on(on_t), .start(start), .out_14(out_14), .out_18(out_15), .out_15(out_16),
    .out_19(out_17), .out_16(out_18), .out_20(out_19), .out_17(out_20), .out_21(out_21),
    .\end (menumega_1_end), .in_6(main_1_out_3), .in_7(main_1_out_5), .in_8(main_1_out_7),
    .in_9(main_1_out_9), .in_10(main_1_out_4), .in_11(main_1_out_6), .in_12(main_1_out_8),
    .in_13(main_1_out_10), .endgame(endGame), .gameover(gameOver));
  menumega menumega_2 (
    .beg(menumega_1_end), .on(on_t), .start(start), .out_14(out_22), .out_18(out_23), .out_15(out_24),
    .out_19(out_25), .out_16(out_26), .out_20(out_27), .out_17(out_28), .out_21(out_29),
    .\end (menumega_2_end), .in_6(main_1_out_11), .in_7(main_1_out_13), .in_8(main_1_out_15),
    .in_9(main_1_out_17), .in_10(main_1_out_12), .in_11(main_1_out_14), .in_12(main_1_out_16),
    .in_13(main_1_out_18), .endgame(endGame), .gameover(gameOver));
  menumega menumega_3 (
    .beg(menumega_2_end), .on(on_t), .start(start), .out_14(out_30), .out_18(out_31), .out_15(out_32),
    .out_19(out_33), .out_16(out_34), .out_20(out_35), .out_17(out_36), .out_21(out_37),
    .\end (menumega_3_end), .in_6(main_1_out_19), .in_7(main_1_out_21), .in_8(main_1_out_23),
    .in_9(main_1_out_25), .in_10(main_1_out_20), .in_11(main_1_out_22), .in_12(main_1_out_24),
    .in_13(main_1_out_26), .endgame(endGame), .gameover(gameOver));
  menumega menumega_4 (
    .beg(menumega_3_end), .on(on_t), .start(start), .out_14(out_38), .out_18(out_39), .out_15(out_40),
    .out_19(out_41), .out_16(out_42), .out_20(out_43), .out_17(out_44), .out_21(out_45),
    .in_6(main_1_out_27), .in_7(main_1_out_29), .in_8(main_1_out_31), .in_9(main_1_out_33),
    .in_10(main_1_out_28), .in_11(main_1_out_30), .in_12(main_1_out_32), .in_13(main_1_out_34),
    .endgame(endGame), .gameover(gameOver));  // open: end

  // Other names for the same wires on the sheet: _0[31:0] = out_14; _1_t[31:0] = out_15; _2_t[31:0] = out_16;
  //   _3_t[31:0] = out_17; _4_t[31:0] = out_18; _5_t[31:0] = out_19; _6_t[31:0] = out_20; _7_t[31:0] = out_21;
  //   _8_t[31:0] = out_22; _9[31:0] = out_23; _10[31:0] = out_24; _11[31:0] = out_25; _12[31:0] = out_26;
  //   _13[31:0] = out_27; _14[31:0] = out_28; _15[31:0] = out_29; _16[31:0] = out_30; _17[31:0] = out_31;
  //   _18[31:0] = out_32; _19[31:0] = out_33; _20[31:0] = out_34; _21[31:0] = out_35; _22[31:0] = out_36;
  //   _23[31:0] = out_37; _24[31:0] = out_38; _25[31:0] = out_39; _26[31:0] = out_40; _27[31:0] = out_41;
  //   _28[31:0] = out_42; _29[31:0] = out_43; _30[31:0] = out_44; _31[31:0] = out_45; eg = endGame; go = gameOver
endmodule

module MAIN (
  input  gameover,
  input  endgame,
  input  start
);

  wire _1_out, _2_out, _3_out, _4_out, _5_out, _6_out, _7_out, _8_out, button_1_out, clock_1_out,
       keyboard_1_avail;
  wire [6:0] keyboard_1_data;
  wire [31:0] pentamenu_1_out_14, pentamenu_1_out_15, pentamenu_1_out_16, pentamenu_1_out_17,
       pentamenu_1_out_18, pentamenu_1_out_19, pentamenu_1_out_20, pentamenu_1_out_21, pentamenu_1_out_22,
       pentamenu_1_out_23, pentamenu_1_out_24, pentamenu_1_out_25, pentamenu_1_out_26, pentamenu_1_out_27,
       pentamenu_1_out_28, pentamenu_1_out_29, pentamenu_1_out_30, pentamenu_1_out_31, pentamenu_1_out_32,
       pentamenu_1_out_33, pentamenu_1_out_34, pentamenu_1_out_35, pentamenu_1_out_36, pentamenu_1_out_37,
       pentamenu_1_out_38, pentamenu_1_out_39, pentamenu_1_out_40, pentamenu_1_out_41, pentamenu_1_out_42,
       pentamenu_1_out_43, pentamenu_1_out_44, pentamenu_1_out_45;

  Clock clock_1 (.out(clock_1_out));
  Keyboard keyboard_1 (
    .clk(clock_1_out), .re(keyboard_1_avail), .avail(keyboard_1_avail), .data(keyboard_1_data));  // open: clr
  Button _8 (.out(_8_out));
  Button _7 (.out(_7_out));
  Button _6 (.out(_6_out));
  Button _5 (.out(_5_out));
  Button _4 (.out(_4_out));
  Button _3 (.out(_3_out));
  Button _2 (.out(_2_out));
  Button _1 (.out(_1_out));
  Button button_1 (.out(button_1_out));
  DotMatrix #(.inputtype("row"), .matrixcols(32), .matrixrows(32)) dotmatrix_1 (
    .row0(pentamenu_1_out_45), .row1(pentamenu_1_out_44), .row2(pentamenu_1_out_43),
    .row3(pentamenu_1_out_42), .row4(pentamenu_1_out_41), .row5(pentamenu_1_out_40),
    .row6(pentamenu_1_out_39), .row7(pentamenu_1_out_38), .row8(pentamenu_1_out_37),
    .row9(pentamenu_1_out_36), .row10(pentamenu_1_out_35), .row11(pentamenu_1_out_34),
    .row12(pentamenu_1_out_33), .row13(pentamenu_1_out_32), .row14(pentamenu_1_out_31),
    .row15(pentamenu_1_out_30), .row16(pentamenu_1_out_29), .row17(pentamenu_1_out_28),
    .row18(pentamenu_1_out_27), .row19(pentamenu_1_out_26), .row20(pentamenu_1_out_25),
    .row21(pentamenu_1_out_24), .row22(pentamenu_1_out_23), .row23(pentamenu_1_out_22),
    .row24(pentamenu_1_out_21), .row25(pentamenu_1_out_20), .row26(pentamenu_1_out_19),
    .row27(pentamenu_1_out_18), .row28(pentamenu_1_out_17), .row29(pentamenu_1_out_16),
    .row30(pentamenu_1_out_15), .row31(pentamenu_1_out_14));
  pentamenu pentamenu_1 (
    .out_14(pentamenu_1_out_14), .out_15(pentamenu_1_out_15), .start(start), .out_16(pentamenu_1_out_16),
    .on(button_1_out), .out_17(pentamenu_1_out_17), .out_18(pentamenu_1_out_18), .out_19(pentamenu_1_out_19),
    .out_20(pentamenu_1_out_20), .endGame(endgame), .gameOver(gameover), .control(keyboard_1_data),
    ._8(_1_out), ._7(_2_out), .out_21(pentamenu_1_out_21), ._6(_3_out), ._5(_4_out), ._4(_5_out),
    ._3(_6_out), ._2(_7_out), ._1(_8_out), .out_22(pentamenu_1_out_22), .out_23(pentamenu_1_out_23),
    .out_24(pentamenu_1_out_24), .out_25(pentamenu_1_out_25), .out_26(pentamenu_1_out_26),
    .out_27(pentamenu_1_out_27), .out_28(pentamenu_1_out_28), .out_29(pentamenu_1_out_29),
    .out_30(pentamenu_1_out_30), .out_31(pentamenu_1_out_31), .out_32(pentamenu_1_out_32),
    .out_33(pentamenu_1_out_33), .out_34(pentamenu_1_out_34), .out_35(pentamenu_1_out_35),
    .out_36(pentamenu_1_out_36), .out_37(pentamenu_1_out_37), .out_38(pentamenu_1_out_38),
    .out_39(pentamenu_1_out_39), .out_40(pentamenu_1_out_40), .out_41(pentamenu_1_out_41),
    .out_42(pentamenu_1_out_42), .out_43(pentamenu_1_out_43), .out_44(pentamenu_1_out_44),
    .out_45(pentamenu_1_out_45));
endmodule

module gameover (
  input  [4:0] in,
  input  isGameOver,
  output [31:0] out
);

  wire decoder_1_out0, decoder_1_out1, decoder_1_out2, decoder_1_out3, decoder_1_out4, decoder_1_out5,
       decoder_1_out6, decoder_1_out7, decoder_1_out8, decoder_1_out9, decoder_1_out10, decoder_1_out11,
       decoder_1_out12, decoder_1_out13, decoder_1_out14, decoder_1_out15, decoder_1_out16, decoder_1_out17,
       decoder_1_out18, decoder_1_out19, decoder_1_out20, decoder_1_out21, decoder_1_out22, decoder_1_out23,
       decoder_1_out24, decoder_1_out25, decoder_1_out26, decoder_1_out27, decoder_1_out28, decoder_1_out29,
       decoder_1_out30, decoder_1_out31;
  wire [31:0] multiplexer_1_out, multiplexer_2_out, multiplexer_3_out, multiplexer_4_out, multiplexer_5_out,
       multiplexer_6_out, multiplexer_7_out, multiplexer_8_out, multiplexer_9_out, multiplexer_10_out,
       multiplexer_11_out, multiplexer_12_out, multiplexer_13_out, multiplexer_14_out, multiplexer_15_out,
       pull_resistor_1_node, pull_resistor_2_node, pull_resistor_3_node;

  Pull_Resistor pull_resistor_1 (.node(pull_resistor_1_node));
  Multiplexer #(.width(32)) multiplexer_1 (
    .in0(32'h1c3e840), .in1(32'h7e187e44), .out(multiplexer_1_out), .sel(isGameOver));  // open: en
  Multiplexer #(.width(32)) multiplexer_2 (
    .in0(32'h2a088c0), .in1(32'h42184048), .out(multiplexer_2_out), .sel(isGameOver));  // open: en
  Multiplexer #(.width(32)) multiplexer_3 (
    .in0(32'h2a089c0), .in1(32'h42247c60), .out(multiplexer_3_out), .sel(isGameOver));  // open: en
  Multiplexer #(.width(32)) multiplexer_4 (
    .in0(32'h6b08940), .in1(32'h2466407c), .out(multiplexer_4_out), .sel(isGameOver));  // open: en
  Multiplexer #(.width(32)) multiplexer_5 (
    .in0(32'h6b08b40), .in1(32'h42424042), .out(multiplexer_5_out), .sel(isGameOver));  // open: en
  Multiplexer #(.width(32)) multiplexer_6 (
    .in0(32'hc988e40), .in1(32'h42c34042), .out(multiplexer_6_out), .sel(isGameOver));  // open: en
  Multiplexer #(.width(32)) multiplexer_7 (
    .in0(32'hc988c40), .in1(32'h7e817e7c), .out(multiplexer_7_out), .sel(isGameOver));  // open: en
  Multiplexer #(.width(32)) multiplexer_8 (
    .in0(32'h80be840), .in1(32'h7e42817e), .out(multiplexer_8_out), .sel(isGameOver));  // open: en
  Pull_Resistor pull_resistor_2 (.node(pull_resistor_2_node));
  Multiplexer #(.width(32)) multiplexer_9 (
    .in0(32'h1f7df00), .in1(32'h43428140), .out(multiplexer_9_out), .sel(isGameOver));  // open: en
  Multiplexer #(.width(32)) multiplexer_10 (
    .in0(32'h145100), .in1(32'h42428140), .out(multiplexer_10_out), .sel(isGameOver));  // open: en
  Multiplexer #(.width(32)) multiplexer_11 (
    .in0(32'h145100), .in1(32'h407e817c), .out(multiplexer_11_out), .sel(isGameOver));  // open: en
  Multiplexer #(.width(32)) multiplexer_12 (
    .in0(32'h1f45100), .in1(32'h40429940), .out(multiplexer_12_out), .sel(isGameOver));  // open: en
  Multiplexer #(.width(32)) multiplexer_13 (
    .in0(32'h1145100), .in1(32'h4242bd40), .out(multiplexer_13_out), .sel(isGameOver));  // open: en
  Multiplexer #(.width(32)) multiplexer_14 (
    .in0(32'h1145100), .in1(32'h4242e740), .out(multiplexer_14_out), .sel(isGameOver));  // open: en
  Multiplexer #(.width(32)) multiplexer_15 (
    .in0(32'h117d100), .in1(32'h7e7ec37e), .out(multiplexer_15_out), .sel(isGameOver));  // open: en
  Pull_Resistor pull_resistor_3 (.node(pull_resistor_3_node));
  Decoder #(.select(5), .disabled(0), .enable("false")) decoder_1 (
    .out0(decoder_1_out0), .out1(decoder_1_out1), .out2(decoder_1_out2), .out3(decoder_1_out3),
    .out4(decoder_1_out4), .out5(decoder_1_out5), .out6(decoder_1_out6), .out7(decoder_1_out7),
    .out8(decoder_1_out8), .out9(decoder_1_out9), .out10(decoder_1_out10), .out11(decoder_1_out11),
    .out12(decoder_1_out12), .out13(decoder_1_out13), .out14(decoder_1_out14), .out15(decoder_1_out15),
    .out16(decoder_1_out16), .out17(decoder_1_out17), .out18(decoder_1_out18), .out19(decoder_1_out19),
    .out20(decoder_1_out20), .out21(decoder_1_out21), .out22(decoder_1_out22), .out23(decoder_1_out23),
    .out24(decoder_1_out24), .out25(decoder_1_out25), .out26(decoder_1_out26), .out27(decoder_1_out27),
    .out28(decoder_1_out28), .out29(decoder_1_out29), .out30(decoder_1_out30), .out31(decoder_1_out31),
    .sel(in));
  assign out = decoder_1_out28 ? pull_resistor_3_node : 32'bz;  // Controlled_Buffer controlled_buffer_1
  assign out = decoder_1_out29 ? pull_resistor_3_node : 32'bz;  // Controlled_Buffer controlled_buffer_2
  assign out = decoder_1_out30 ? pull_resistor_3_node : 32'bz;  // Controlled_Buffer controlled_buffer_3
  assign out = decoder_1_out31 ? pull_resistor_3_node : 32'bz;  // Controlled_Buffer controlled_buffer_4
  assign out = decoder_1_out26 ? multiplexer_14_out : 32'bz;  // Controlled_Buffer controlled_buffer_5
  assign out = decoder_1_out27 ? multiplexer_15_out : 32'bz;  // Controlled_Buffer controlled_buffer_6
  assign out = decoder_1_out23 ? multiplexer_11_out : 32'bz;  // Controlled_Buffer controlled_buffer_7
  assign out = decoder_1_out24 ? multiplexer_12_out : 32'bz;  // Controlled_Buffer controlled_buffer_8
  assign out = decoder_1_out25 ? multiplexer_13_out : 32'bz;  // Controlled_Buffer controlled_buffer_9
  assign out = decoder_1_out19 ? pull_resistor_2_node : 32'bz;  // Controlled_Buffer controlled_buffer_10
  assign out = decoder_1_out20 ? pull_resistor_2_node : 32'bz;  // Controlled_Buffer controlled_buffer_11
  assign out = decoder_1_out21 ? multiplexer_9_out : 32'bz;  // Controlled_Buffer controlled_buffer_12
  assign out = decoder_1_out22 ? multiplexer_10_out : 32'bz;  // Controlled_Buffer controlled_buffer_13
  assign out = decoder_1_out15 ? pull_resistor_2_node : 32'bz;  // Controlled_Buffer controlled_buffer_14
  assign out = decoder_1_out16 ? pull_resistor_2_node : 32'bz;  // Controlled_Buffer controlled_buffer_15
  assign out = decoder_1_out17 ? pull_resistor_2_node : 32'bz;  // Controlled_Buffer controlled_buffer_16
  assign out = decoder_1_out18 ? pull_resistor_2_node : 32'bz;  // Controlled_Buffer controlled_buffer_17
  assign out = decoder_1_out12 ? multiplexer_8_out : 32'bz;  // Controlled_Buffer controlled_buffer_18
  assign out = decoder_1_out13 ? pull_resistor_2_node : 32'bz;  // Controlled_Buffer controlled_buffer_19
  assign out = decoder_1_out14 ? pull_resistor_2_node : 32'bz;  // Controlled_Buffer controlled_buffer_20
  assign out = decoder_1_out9 ? multiplexer_5_out : 32'bz;  // Controlled_Buffer controlled_buffer_21
  assign out = decoder_1_out10 ? multiplexer_6_out : 32'bz;  // Controlled_Buffer controlled_buffer_22
  assign out = decoder_1_out11 ? multiplexer_7_out : 32'bz;  // Controlled_Buffer controlled_buffer_23
  assign out = decoder_1_out5 ? multiplexer_1_out : 32'bz;  // Controlled_Buffer controlled_buffer_24
  assign out = decoder_1_out6 ? multiplexer_2_out : 32'bz;  // Controlled_Buffer controlled_buffer_25
  assign out = decoder_1_out7 ? multiplexer_3_out : 32'bz;  // Controlled_Buffer controlled_buffer_26
  assign out = decoder_1_out8 ? multiplexer_4_out : 32'bz;  // Controlled_Buffer controlled_buffer_27
  assign out = decoder_1_out2 ? pull_resistor_1_node : 32'bz;  // Controlled_Buffer controlled_buffer_28
  assign out = decoder_1_out3 ? pull_resistor_1_node : 32'bz;  // Controlled_Buffer controlled_buffer_29
  assign out = decoder_1_out4 ? pull_resistor_1_node : 32'bz;  // Controlled_Buffer controlled_buffer_30
  assign out = decoder_1_out0 ? pull_resistor_1_node : 32'bz;  // Controlled_Buffer controlled_buffer_31
  assign out = decoder_1_out1 ? pull_resistor_1_node : 32'bz;  // Controlled_Buffer controlled_buffer_32
endmodule

module oradd8 (
  input  [7:0] in,
  output out
);

  or or_1 (out, in[0], in[1], in[2], in[3], in[4], in[5], in[6], in[7]);
endmodule

module oradd32 (
  input  [31:0] in,
  output out
);

  or or_1 (out, in[0], in[1], in[2], in[3], in[4], in[5], in[6], in[7], in[8], in[9], in[10], in[11], in[12], in[13], in[14], in[15], in[16], in[17], in[18], in[19], in[20], in[21], in[22], in[23], in[24], in[25], in[26], in[27], in[28], in[29], in[30], in[31]);
endmodule

module sub (
  input  [7:0] A,
  input  [7:0] B,
  output [7:0] R
);

  wire [7:0] negator_1_out;

  Negator negator_1 (.in(B), .out(negator_1_out));
  Adder adder_1 (.a(A), .b(negator_1_out), .out(R));  // open: cin, cout
endmodule

module got1 (
  input  in_1,
  output out_2
);

  wire clock_1_out;

  D_Flip_Flop d_ff_1 (.Q(out_2), .preset(in_1), .reset(clock_1_out));  // open: clk, D, Qn, en
  Clock #(.highDuration(2), .lowDuration(2)) clock_1 (.out(clock_1_out));

  // Notes on the sheet:
  //   У этойсхемы частота в 2 раза меньше, для того чтобы поймать мгновенную единичку
endmodule

module dtriglit (
  input  in,
  output out
);

  wire d_ff_1_q, undriven;

  D_Flip_Flop d_ff_1 (.D(undriven), .Q(d_ff_1_q), .preset(undriven));  // open: clk, Qn, en, reset
  not not_1 (out, d_ff_1_q);
endmodule
module enemies (
  input  in_1,
  input  [7:0] enem,
  input  [7:0] in_arr0,
  input  [7:0] in_arr1,
  input  [7:0] in_arr2,
  input  [7:0] in_arr3,
  input  [4:0] enemynum,
  output [7:0] out
);

  wire _1_prime_prime_prime, _2_prime_prime_prime, _3_prime_prime_prime, _4_prime_prime_prime,
       _11_prime_prime_prime, _12_prime_prime_prime, _13_prime_prime_prime, _14_prime_prime_prime, and_1_out,
       and_2_out, and_3_out, and_4_out, and_5_out, and_6_out, and_7_out, cdm_8_mark5_1_data_inst,
       cdm_8_mark5_1_mem_cycle, cdm_8_mark5_1_mem_read, clk, clr, comparator_1_eq, comparator_2_eq,
       comparator_3_eq, comparator_4_eq, comparator_5_eq, comparator_6_eq, comparator_7_eq, comparator_8_eq,
       comparator_9_eq, comparator_10_eq, comparator_11_eq, comparator_12_eq, comparator_13_eq,
       comparator_14_eq, controlled_buffer_17_out, d_ff_1_q, decoder_1_out0, decoder_1_out1, enemOn, IN,
       init, L, not_2_out, not_3_out, not_4_out, or_1_out, or_2_out, or_3_out, or_4_out, or_5_out, or_6_out,
       or_8_out, OUT_t, R, START, stringOn;
  wire [1:0] priority_encoder_1_out;
  wire [2:0] counter_2_q;
  wire [3:0] counter_3_q;
  wire [4:0] counter_1_q, inc5_1_r;
  wire [7:0] _1_prime, _1_prime_prime, _2_prime, _2_prime_prime, _3_prime, _3_prime_prime, _4_prime,
       _4_prime_prime, addr, arr0, arr1, arr2, arr3, cdm_8_mark5_1_data_out, cdm_8_mark5_1_ps,
       cdm_8_mark5_1_r0, cdm_8_mark5_1_r1, cdm_8_mark5_1_r2, cdm_8_mark5_1_r3, cdm_8_mark5_1_sp,
       controlled_buffer_18_out, controlled_buffer_19_out, controlled_buffer_20_out, enem_t, io_data,
       ram_1_data, register_33_q, register_34_q, register_35_q, register_36_q, sign;
  wire [31:0] _0, _0_, _1, _1_, _2, _2_, _3, _3_, _4, _4_, _5, _5_, _6, _6_, _7, _7_, _8, _8_, _9, _10, _11,
       _12, _13, _14, _15, multiplexer_1_out, multiplexer_2_out, pull_resistor_1_node, shifterdown_1_out_20,
       shifterdown_1_out_21, shifterdown_1_out_22, shifterdown_1_out_23, shifterdown_1_out_24,
       shifterdown_1_out_25, shifterdown_1_out_26, shifterdown_1_out_27, shifterdown_1_out_28,
       shifterdown_1_out_29, shifterdown_1_out_30, shifterdown_1_out_31, shifterdown_1_out_32,
       shifterdown_1_out_33, shifterdown_1_out_34, \shifterdown_1_выход_0 , undriven, undriven_2, undriven_3,
       undriven_4, undriven_5, undriven_6, undriven_7, undriven_8, undriven_9, undriven_10, undriven_11,
       undriven_12, undriven_13, undriven_14, undriven_15, undriven_16, undriven_17, undriven_18,
       undriven_19, undriven_20, undriven_21, undriven_22, undriven_23, undriven_24, undriven_25,
       undriven_26, undriven_27, undriven_28, undriven_29, undriven_30, \попадание_1_out ;

  Register register_1 (.D(_3_prime), .en(init), .Q(_2_[31:24]), .clk(init), .clr(_1_prime_prime_prime));
  Register register_2 (.D(_3_prime), .en(init), .Q(_7_[31:24]), .clk(init), .clr(_11_prime_prime_prime));
  Register register_3 (.D(_3_prime_prime), .en(init), .Q(_2_[23:16]), .clk(init), .clr(_2_prime_prime_prime));
  Register register_4 (.D(_3_prime_prime), .en(init), .Q(_7_[23:16]), .clk(init), .clr(_12_prime_prime_prime));
  Counter #(.width(5), .max('h1f)) counter_1 (
    .D(enemynum), .Q(counter_1_q), .clk(init));  // open: load, count, carry, clr
  \попадание  \u_попадание_1  (.OUT(\попадание_1_out ), .A(multiplexer_1_out), .B(multiplexer_2_out));
  \монстр__майн  \u_монстр_майн_1  (
    .\_4строка (_4_prime_prime), .\_3строка (_3_prime_prime), .\_2строка (_2_prime_prime),
    .\_1строка (_1_prime_prime));
  Register register_5 (.D(_3_prime_prime), .en(init), .Q(_2_[15:8]), .clk(init), .clr(_3_prime_prime_prime));
  Register register_6 (.D(_3_prime_prime), .en(init), .Q(_7_[15:8]), .clk(init), .clr(_13_prime_prime_prime));
  Register register_7 (.D(_4_prime), .en(init), .Q(_3_[7:0]), .clk(init), .clr(_4_prime_prime_prime));
  Register register_8 (.D(_4_prime_prime), .en(init), .Q(_3_[15:8]), .clk(init), .clr(_3_prime_prime_prime));
  Register register_9 (.D(_4_prime_prime), .en(init), .Q(_3_[23:16]), .clk(init), .clr(_2_prime_prime_prime));
  Register register_10 (.D(_4_prime), .en(init), .Q(_3_[31:24]), .clk(init), .clr(_1_prime_prime_prime));
  Clock clock_1 (.out(init));
  Register register_11 (.D(_3_prime), .en(init), .Q(_2_[7:0]), .clk(init), .clr(_4_prime_prime_prime));
  Register register_12 (.D(_3_prime), .en(init), .Q(_7_[7:0]), .clk(init), .clr(_14_prime_prime_prime));
  Register register_13 (.D(_4_prime), .en(init), .Q(_8_[7:0]), .clk(init), .clr(_14_prime_prime_prime));
  Register register_14 (.D(_4_prime_prime), .en(init), .Q(_8_[15:8]), .clk(init), .clr(_13_prime_prime_prime));
  Register register_15 (.D(_4_prime_prime), .en(init), .Q(_8_[23:16]), .clk(init), .clr(_12_prime_prime_prime));
  Register register_16 (.D(_4_prime), .en(init), .Q(_8_[31:24]), .clk(init), .clr(_11_prime_prime_prime));
  Multiplexer #(.select(5), .width(32)) multiplexer_1 (
    .in0(undriven), .in1(undriven_2), .in2(undriven_3), .in3(undriven_4), .in4(undriven_5), .in5(undriven_6),
    .in6(undriven_29), .in7(undriven_7), .in8(undriven_8), .in9(undriven_9), .in10(undriven_10),
    .in11(undriven_11), .in12(undriven_12), .in13(undriven_13), .in14(undriven_14), .in15(undriven_15),
    .in16(undriven_16), .in17(undriven_17), .in18(undriven_18), .in19(undriven_30), .in20(undriven_19),
    .in21(undriven_20), .in22(undriven_21), .in23(undriven_22), .in24(undriven_23), .in25(undriven_24),
    .in26(undriven_25), .in27(undriven_26), .in28(undriven_27), .in29(undriven_28), .out(multiplexer_1_out),
    .sel(counter_1_q));  // open: in30, in31, en
  inc5 inc5_1 (.X(counter_1_q), .R(inc5_1_r));  // open: Cout
  Multiplexer #(.select(5), .width(32)) multiplexer_2 (
    .in0(undriven), .in1(undriven_2), .in2(undriven_3), .in3(undriven_4), .in4(undriven_5), .in5(undriven_6),
    .in6(undriven_29), .in7(undriven_7), .in8(undriven_8), .in9(undriven_9), .in10(undriven_10),
    .in11(undriven_11), .in12(undriven_12), .in13(undriven_13), .in14(undriven_14), .in15(undriven_15),
    .in16(undriven_16), .in17(undriven_17), .in18(undriven_18), .in19(undriven_30), .in20(undriven_19),
    .in21(undriven_20), .in22(undriven_21), .in23(undriven_22), .in24(undriven_23), .in25(undriven_24),
    .in26(undriven_25), .in27(undriven_26), .in28(undriven_27), .in29(undriven_28), .out(multiplexer_2_out),
    .sel(inc5_1_r));  // open: in30, in31, en
  \монстр__т  \u_монстр_т_1  (
    .\_4строка (_4_prime), .\_3строка (_3_prime), .\_2строка (_2_prime), .\_1строка (_1_prime));
  Counter #(.width(3), .max('h5)) counter_2 (.Q(counter_2_q), .clk(clk), .clr(START));  // open: load, D, count, carry
  Clock clock_2 (.out(clk));
  Register register_17 (.D(_2_prime), .en(init), .Q(_6_[7:0]), .clk(init), .clr(_14_prime_prime_prime));
  Register register_18 (.D(_2_prime_prime), .en(init), .Q(_6_[15:8]), .clk(init), .clr(_13_prime_prime_prime));
  Register register_19 (.D(_2_prime_prime), .en(init), .Q(_6_[23:16]), .clk(init), .clr(_12_prime_prime_prime));
  Register register_20 (.D(_2_prime), .en(init), .Q(_6_[31:24]), .clk(init), .clr(_11_prime_prime_prime));
  Comparator #(.width(3)) comparator_1 (.a(counter_2_q), .b(3'b010), .eq(comparator_1_eq));  // open: gt, lt
  Comparator #(.width(3)) comparator_2 (.a(counter_2_q), .b(3'b101), .eq(comparator_2_eq));  // open: gt, lt
  Comparator #(.width(3)) comparator_3 (.a(counter_2_q), .b(3'b001), .eq(comparator_3_eq));  // open: gt, lt
  Comparator #(.width(3)) comparator_4 (.a(counter_2_q), .b(3'b011), .eq(comparator_4_eq));  // open: gt, lt
  Comparator #(.width(3)) comparator_5 (.a(counter_2_q), .b(3'b100), .eq(comparator_5_eq));  // open: gt, lt
  Comparator #(.width(3)) comparator_6 (.a(counter_2_q), .b(3'b000), .eq(comparator_6_eq));  // open: gt, lt
  Counter #(.width(4), .max('hf)) counter_3 (
    .Q(counter_3_q), .clk(or_1_out), .clr(START));  // open: load, D, count, carry
  or or_1 (or_1_out, comparator_1_eq, comparator_2_eq);
  Counter #(.width(1), .max('h1)) counter_4 (.Q(L), .clk(or_2_out), .clr(START));  // open: load, D, count, carry
  or or_2 (or_2_out, comparator_3_eq, comparator_4_eq);
  Counter #(.width(1), .max('h1)) counter_5 (.Q(R), .clk(or_3_out), .clr(START));  // open: load, D, count, carry
  or or_3 (or_3_out, comparator_5_eq, comparator_6_eq);
  Register register_21 (.D(_2_prime), .en(init), .Q(_1_[7:0]), .clk(init), .clr(_4_prime_prime_prime));
  Register register_22 (.D(_2_prime_prime), .en(init), .Q(_1_[15:8]), .clk(init), .clr(_3_prime_prime_prime));
  Register register_23 (.D(_2_prime_prime), .en(init), .Q(_1_[23:16]), .clk(init), .clr(_2_prime_prime_prime));
  Register register_24 (.D(_2_prime), .en(init), .Q(_1_[31:24]), .clk(init), .clr(_1_prime_prime_prime));
  Comparator comparator_7 (.a(sign), .b(8'hb), .eq(comparator_7_eq));  // open: gt, lt
  Comparator comparator_8 (.a(sign), .b(8'h1a), .eq(comparator_8_eq));  // open: gt, lt
  Register register_25 (.D(_1_prime), .en(init), .Q(_5_[7:0]), .clk(init), .clr(_14_prime_prime_prime));
  Register register_26 (.D(_1_prime_prime), .en(init), .Q(_5_[15:8]), .clk(init), .clr(_13_prime_prime_prime));
  Register register_27 (.D(_1_prime_prime), .en(init), .Q(_5_[23:16]), .clk(init), .clr(_12_prime_prime_prime));
  Register register_28 (.D(_1_prime), .en(init), .Q(_5_[31:24]), .clk(init), .clr(_11_prime_prime_prime));
  not not_1 (START, in_1);
  Comparator comparator_9 (.a(sign), .b(8'h33), .eq(comparator_9_eq));  // open: gt, lt
  or or_4 (or_4_out, comparator_7_eq, comparator_8_eq);
  Pull_Resistor pull_resistor_1 (.node(pull_resistor_1_node));
  and and_1 (and_1_out, ~L, ~R);  // AND_Gate
  assign _11 = and_1_out ? shifterdown_1_out_30 : 32'bz;  // Controlled_Buffer controlled_buffer_1
  assign _10 = and_1_out ? shifterdown_1_out_29 : 32'bz;  // Controlled_Buffer controlled_buffer_2
  assign _9 = and_1_out ? shifterdown_1_out_28 : 32'bz;  // Controlled_Buffer controlled_buffer_3
  assign _14 = and_1_out ? shifterdown_1_out_33 : 32'bz;  // Controlled_Buffer controlled_buffer_4
  assign _13 = and_1_out ? shifterdown_1_out_32 : 32'bz;  // Controlled_Buffer controlled_buffer_5
  assign _12 = and_1_out ? shifterdown_1_out_31 : 32'bz;  // Controlled_Buffer controlled_buffer_6
  assign _15 = and_1_out ? shifterdown_1_out_34 : 32'bz;  // Controlled_Buffer controlled_buffer_7
  or or_5 (or_5_out, comparator_9_eq, comparator_7_eq);
  Comparator comparator_10 (.a(addr), .b(8'hc0), .eq(comparator_10_eq));  // open: gt, lt
  Comparator comparator_11 (.a(addr), .b(8'hc1), .eq(comparator_11_eq));  // open: gt, lt
  Comparator comparator_12 (.a(addr), .b(8'hc2), .eq(comparator_12_eq));  // open: gt, lt
  Comparator comparator_13 (.a(addr), .b(8'hc3), .eq(comparator_13_eq));  // open: gt, lt
  Register register_29 (.D(_1_prime), .en(init), .Q(_0_[7:0]), .clk(init), .clr(_4_prime_prime_prime));
  Register register_30 (.D(_1_prime_prime), .en(init), .Q(_0_[15:8]), .clk(init), .clr(_3_prime_prime_prime));
  Register register_31 (.D(_1_prime_prime), .en(init), .Q(_0_[23:16]), .clk(init), .clr(_2_prime_prime_prime));
  Register register_32 (.D(_1_prime), .en(init), .Q(_0_[31:24]), .clk(init), .clr(_1_prime_prime_prime));
  Pull_Resistor pull_resistor_2 (.node(_4_));
  assign _1 = and_1_out ? shifterdown_1_out_20 : 32'bz;  // Controlled_Buffer controlled_buffer_8
  assign _3 = and_1_out ? shifterdown_1_out_22 : 32'bz;  // Controlled_Buffer controlled_buffer_9
  assign _2 = and_1_out ? shifterdown_1_out_21 : 32'bz;  // Controlled_Buffer controlled_buffer_10
  assign _6 = and_1_out ? shifterdown_1_out_25 : 32'bz;  // Controlled_Buffer controlled_buffer_11
  assign _4 = and_1_out ? shifterdown_1_out_23 : 32'bz;  // Controlled_Buffer controlled_buffer_12
  assign _5 = and_1_out ? shifterdown_1_out_24 : 32'bz;  // Controlled_Buffer controlled_buffer_13
  assign _7 = and_1_out ? shifterdown_1_out_26 : 32'bz;  // Controlled_Buffer controlled_buffer_14
  assign _8 = and_1_out ? shifterdown_1_out_27 : 32'bz;  // Controlled_Buffer controlled_buffer_15
  Button button_1 (.out(clr));
  and and_2 (and_2_out, comparator_10_eq, or_5_out);
  and and_3 (and_3_out, comparator_11_eq, or_5_out);
  and and_4 (and_4_out, comparator_12_eq, or_5_out);
  and and_5 (and_5_out, comparator_13_eq, or_5_out);
  shifterDown shifterdown_1 (
    .\Вход_0 (_0_), .\Выход_0 (\shifterdown_1_выход_0 ), .in_2(_1_), .out_20(shifterdown_1_out_20),
    .in_3(counter_3_q), .in_4(_2_), .out_21(shifterdown_1_out_21), .in_6(_3_), .out_22(shifterdown_1_out_22),
    .in_7(_4_), .out_23(shifterdown_1_out_23), .in_8(_5_), .out_24(shifterdown_1_out_24), .in_9(_6_),
    .out_25(shifterdown_1_out_25), .in_10(_7_), .out_26(shifterdown_1_out_26), .in_11(_8_),
    .out_27(shifterdown_1_out_27), .in_12(pull_resistor_1_node), .out_28(shifterdown_1_out_28),
    .in_13(pull_resistor_1_node), .out_29(shifterdown_1_out_29), .in_14(pull_resistor_1_node),
    .out_30(shifterdown_1_out_30), .in_15(pull_resistor_1_node), .out_31(shifterdown_1_out_31),
    .in_16(pull_resistor_1_node), .out_32(shifterdown_1_out_32), .in_17(pull_resistor_1_node),
    .out_33(shifterdown_1_out_33), .in_18(pull_resistor_1_node), .out_34(shifterdown_1_out_34), .En(in_1));
  ShifterRight shifterright_1 (
    .\Вход_0 (\shifterdown_1_выход_0 ), .out_18(_0), .in_2(shifterdown_1_out_20), .out_19(_1),
    .in_3(shifterdown_1_out_21), .out_20(_2), .in_4(shifterdown_1_out_22), .out_21(_3),
    .in_5(shifterdown_1_out_23), .out_22(_4), .in_6(shifterdown_1_out_24), .out_23(_5),
    .in_7(shifterdown_1_out_25), .out_24(_6), .in_8(shifterdown_1_out_26), .out_25(_7),
    .in_9(shifterdown_1_out_27), .out_26(_8), .in_10(shifterdown_1_out_28), .out_27(_9),
    .in_11(shifterdown_1_out_29), .out_28(_10), .in_12(shifterdown_1_out_30), .out_29(_11),
    .in_13(shifterdown_1_out_31), .out_30(_12), .in_14(shifterdown_1_out_32), .out_31(_13),
    .in_15(shifterdown_1_out_33), .out_32(_14), .in_16(shifterdown_1_out_34), .out_33(_15), .in_17(R));
  ShifterLeft shifterleft_1 (
    .\Вход_0 (\shifterdown_1_выход_0 ), .out_18(_0), .in_2(shifterdown_1_out_20), .out_19(_1),
    .in_3(shifterdown_1_out_21), .out_20(_2), .in_4(shifterdown_1_out_22), .out_21(_3),
    .in_5(shifterdown_1_out_23), .out_22(_4), .in_6(shifterdown_1_out_24), .out_23(_5),
    .in_7(shifterdown_1_out_25), .out_24(_6), .in_8(shifterdown_1_out_26), .out_25(_7),
    .in_9(shifterdown_1_out_27), .out_26(_8), .in_10(shifterdown_1_out_28), .out_27(_9),
    .in_11(shifterdown_1_out_29), .out_28(_10), .in_12(shifterdown_1_out_30), .out_29(_11),
    .in_13(shifterdown_1_out_31), .out_30(_12), .in_14(shifterdown_1_out_32), .out_31(_13),
    .in_15(shifterdown_1_out_33), .out_32(_14), .in_16(shifterdown_1_out_34), .out_33(_15), .in_17(L));
  assign _0 = and_1_out ? \shifterdown_1_выход_0  : 32'bz;  // Controlled_Buffer controlled_buffer_16
  D_Flip_Flop d_ff_1 (.Q(d_ff_1_q), .preset(clr));  // open: clk, D, Qn, en, reset
  Comparator comparator_14 (.a(addr), .b(8'hc4), .eq(comparator_14_eq));  // open: gt, lt
  and and_6 (and_6_out, addr[4], addr[5], addr[6], addr[7], decoder_1_out1);
  Clock clock_3 (.out(clk));
  // Probe on cdm_8_mark5_1_r3
  // Probe on cdm_8_mark5_1_r2
  // Probe on cdm_8_mark5_1_r1
  // Probe on cdm_8_mark5_1_r0
  assign controlled_buffer_17_out = d_ff_1_q ? clk : 1'bz;  // Controlled_Buffer controlled_buffer_17
  Priority_Encoder #(.select(2)) priority_encoder_1 (
    .in0(and_2_out), .in1(and_3_out), .in2(and_4_out), .in3(and_5_out), .out(priority_encoder_1_out));  // open: gs, en_out, en_in
  or or_6 (or_6_out, and_5_out, and_4_out, and_3_out, and_2_out);
  and and_7 (and_7_out, decoder_1_out1, ~and_6_out);  // AND_Gate
  // Probe on cdm_8_mark5_1_sp
  // Probe on sign
  // Probe on cdm_8_mark5_1_ps
  CdM_8_mark5 cdm_8_mark5_1 (
    .clock(controlled_buffer_17_out), .addr(addr), .mem_read(cdm_8_mark5_1_mem_read),
    .mem_cycle(cdm_8_mark5_1_mem_cycle), .data_inst(cdm_8_mark5_1_data_inst),
    .data_out(cdm_8_mark5_1_data_out), .data_in(controlled_buffer_19_out), .r0(cdm_8_mark5_1_r0),
    .r1(cdm_8_mark5_1_r1), .r2(cdm_8_mark5_1_r2), .r3(cdm_8_mark5_1_r3), .PC(sign), .SP(cdm_8_mark5_1_sp),
    .PS(cdm_8_mark5_1_ps), .reset(clr));  // open: IAck, IRQ, vec
  and and_8 (OUT_t, comparator_9_eq, comparator_14_eq);
  and and_9 (stringOn, or_4_out, or_6_out);
  and and_10 (enemOn, or_4_out, comparator_14_eq);
  Decoder #(.disabled(0)) decoder_1 (
    .out0(decoder_1_out0), .out1(decoder_1_out1), .sel(cdm_8_mark5_1_data_inst), .en(cdm_8_mark5_1_mem_cycle));
  not not_2 (not_2_out, cdm_8_mark5_1_mem_read);
  assign controlled_buffer_18_out = not_2_out ? cdm_8_mark5_1_data_out : 8'bz;  // Controlled_Buffer controlled_buffer_18
  assign controlled_buffer_19_out = cdm_8_mark5_1_mem_read ? controlled_buffer_18_out : 8'bz;  // Controlled_Buffer controlled_buffer_19
  or or_7 (IN, stringOn, enemOn);
  or or_8 (or_8_out, clr, OUT_t);
  assign controlled_buffer_20_out = IN ? io_data : 8'bz;  // Controlled_Buffer controlled_buffer_20
  assign io_data = OUT_t ? controlled_buffer_18_out : 8'bz;  // Controlled_Buffer controlled_buffer_21
  Register register_33 (.D(arr0), .en(clr), .Q(register_33_q), .clk(clk));  // open: clr
  Register register_34 (.D(arr1), .en(clr), .Q(register_34_q), .clk(clk));  // open: clr
  Register register_35 (.D(arr2), .en(clr), .Q(register_35_q), .clk(clk));  // open: clr
  Register register_36 (.D(arr3), .en(clr), .Q(register_36_q), .clk(clk));  // open: clr
  assign enem_t = OUT_t ? io_data : 8'bz;  // Controlled_Buffer controlled_buffer_22
  // Probe on addr
  Register register_37 (.D(enem_t), .en(or_8_out), .Q(out), .clk(clk));  // open: clr
  assign io_data = enemOn ? out : 8'bz;  // Controlled_Buffer controlled_buffer_23
  DotMatrix #(.inputtype("row"), .matrixcols(32), .matrixrows(32)) dotmatrix_1 (
    .row0(_0), .row1(_1), .row2(_2), .row3(_3), .row4(_4), .row5(_5), .row6(_6), .row7(_7), .row8(_8),
    .row9(_9), .row10(_10), .row11(_11), .row12(_12), .row13(_13), .row14(_14), .row15(_15));  // open: row16, row17, row18, row19, row20, row21, row22, row23, row24, row25, row26, row27, row28, row29, row30, row31
  assign controlled_buffer_18_out = IN ? controlled_buffer_20_out : 8'bz;  // Controlled_Buffer controlled_buffer_24
  not not_3 (not_3_out, clk);
  // Probe on controlled_buffer_18_out
  // Probe on controlled_buffer_18_out
  Multiplexer #(.select(2), .width(8)) multiplexer_3 (
    .in0(register_33_q), .in1(register_34_q), .in2(register_35_q), .in3(register_36_q), .out(io_data),
    .sel(priority_encoder_1_out), .en(stringOn));
  assign enem_t = clr ? enem : 8'bz;  // Controlled_Buffer controlled_buffer_25
  assign arr0 = clr ? in_arr0 : 8'bz;  // Controlled_Buffer controlled_buffer_26
  assign arr1 = clr ? in_arr1 : 8'bz;  // Controlled_Buffer controlled_buffer_27
  assign arr2 = clr ? in_arr2 : 8'bz;  // Controlled_Buffer controlled_buffer_28
  assign arr3 = clr ? in_arr3 : 8'bz;  // Controlled_Buffer controlled_buffer_29
  not not_4 (not_4_out, IN);
  // Probe on ram_1_data
  RAM #(.bus("separate")) ram_1 (
    .addr(addr), .din(controlled_buffer_20_out), .data(ram_1_data), .str(IN), .sel(and_7_out),
    .clk(not_3_out), .ld(cdm_8_mark5_1_mem_read), .clr(clr));
  assign controlled_buffer_18_out = not_4_out ? ram_1_data : 8'bz;  // Controlled_Buffer controlled_buffer_30
  ROM rom_1 (.addr(addr), .data(controlled_buffer_18_out), .sel(decoder_1_out0));
  assign {_1_prime_prime_prime, _2_prime_prime_prime, _3_prime_prime_prime, _4_prime_prime_prime, _11_prime_prime_prime, _12_prime_prime_prime, _13_prime_prime_prime, _14_prime_prime_prime} = ~enem;  // NOT_Gate not_5, 8 bits wide

  // Other names for the same wires on the sheet: IOaddr[3:0] = addr[3:0]

  // Notes on the sheet:
  //   V
  //   >
  //   <
  //   чтение
  //   запись
  //   Адреса массива
  //   Триггер на попадание
  //   Адрес байтов врагов
  //   contents of rom_1 (hex, n*v repeats v):
  //   d1 c0 d0 0 d2 3 7 a eb 15 bd 5 e0 10 ee 15 8f 8c 8a ee 7 d1 1 d2 c4 ba 0 e0 21 25 88 ee 1a 7 4b f e1
  //   2f d0 4 0 e0 2f 25 88 ee 28 66 d0 c4 a2 d4 140*0 10 0 0 0 50
endmodule

module \сдвиги__не_используется  (
  input  cntl,
  input  [31:0] in_2,
  input  cntl_2,
  input  [31:0] in_4,
  input  in_5,
  input  in_6,
  output of,
  output [31:0] out_8
);

  wire and_1_out, comparator_1_eq, counter_1_carry, not_1_out, or_1_out, \и ;
  wire [5:0] counter_2_q;
  wire [7:0] counter_1_q;
  wire [31:0] multiplexer_1_out, pull_resistor_1_node, shift_register_1_q0, shift_register_1_q1,
       shift_register_1_q2, shift_register_1_q3, shift_register_1_q4, shift_register_1_q5,
       shift_register_1_q6, shift_register_2_q31, shift_register_3_q0;

  Clock clock_1 (.out(\и ));
  Multiplexer #(.width(32)) multiplexer_1 (
    .in0(in_2), .in1(pull_resistor_1_node), .out(multiplexer_1_out), .sel(counter_1_carry));  // open: en
  Counter #(.max('h5)) counter_1 (
    .count(\и ), .Q(counter_1_q), .carry(counter_1_carry), .clk(\и ));  // open: load, D, clr
  Register #(.width(32)) register_1 (.D(multiplexer_1_out), .en(or_1_out), .Q(out_8), .clk(or_1_out));  // open: clr
  or or_1 (or_1_out, counter_1_carry, \и );
  Comparator comparator_1 (.a(counter_1_q), .b(8'h4), .eq(comparator_1_eq));  // open: gt, lt
  Counter #(.width(6), .max('h3f)) counter_2 (
    .count(counter_1_carry), .Q(counter_2_q));  // open: load, D, carry, clk, clr
  and and_1 (and_1_out, counter_2_q[0], 1'b1);
  Pull_Resistor pull_resistor_1 (.node(pull_resistor_1_node));
  Shift_Register #(.width(32), .length(32), .trigger("falling")) shift_register_1 (
    .clk(in_6), .load(in_5), .d0(in_4), .q0(shift_register_1_q0), .d1(in_4), .q1(shift_register_1_q1),
    .d2(in_4), .q2(shift_register_1_q2), .d3(in_4), .q3(shift_register_1_q3), .q4(shift_register_1_q4),
    .q5(shift_register_1_q5), .q6(shift_register_1_q6));  // open: shift, in, out, clr, d4, d5, d6, d7, q7, d8, q8, d9, q9, d10, q10, d11, q11, d12, q12, d13, q13, d14, q14, d15, q15, d16, q16, d17, q17, d18, q18, d19, q19, d20, q20, d21, q21, d22, q22, d23, q23, d24, q24, d25, q25, d26, q26, d27, q27, d28, q28, d29, q29, d30, q30, d31, q31
  Shift_Register #(.length(32), .trigger("falling")) shift_register_2 (
    .shift(counter_1_carry), .clk(\и ), .load(comparator_1_eq), .d0(out_8[31]),
    .q0(shift_register_2_q31[31]), .d1(out_8[30]), .q1(shift_register_2_q31[30]), .d2(out_8[29]),
    .q2(shift_register_2_q31[29]), .d3(out_8[28]), .q3(shift_register_2_q31[28]), .d4(out_8[27]),
    .q4(shift_register_2_q31[27]), .d5(out_8[26]), .q5(shift_register_2_q31[26]), .d6(out_8[25]),
    .q6(shift_register_2_q31[25]), .d7(out_8[24]), .q7(shift_register_2_q31[24]), .d8(out_8[23]),
    .q8(shift_register_2_q31[23]), .d9(out_8[22]), .q9(shift_register_2_q31[22]), .d10(out_8[21]),
    .q10(shift_register_2_q31[21]), .d11(out_8[20]), .q11(shift_register_2_q31[20]), .d12(out_8[19]),
    .q12(shift_register_2_q31[19]), .d13(out_8[18]), .q13(shift_register_2_q31[18]), .d14(out_8[17]),
    .q14(shift_register_2_q31[17]), .d15(out_8[16]), .q15(shift_register_2_q31[16]), .d16(out_8[15]),
    .q16(shift_register_2_q31[15]), .d17(out_8[14]), .q17(shift_register_2_q31[14]), .d18(out_8[13]),
    .q18(shift_register_2_q31[13]), .d19(out_8[12]), .q19(shift_register_2_q31[12]), .d20(out_8[11]),
    .q20(shift_register_2_q31[11]), .d21(out_8[10]), .q21(shift_register_2_q31[10]), .d22(out_8[9]),
    .q22(shift_register_2_q31[9]), .d23(out_8[8]), .q23(shift_register_2_q31[8]), .d24(out_8[7]),
    .q24(shift_register_2_q31[7]), .d25(out_8[6]), .q25(shift_register_2_q31[6]), .d26(out_8[5]),
    .q26(shift_register_2_q31[5]), .d27(out_8[4]), .q27(shift_register_2_q31[4]), .d28(out_8[3]),
    .q28(shift_register_2_q31[3]), .d29(out_8[2]), .q29(shift_register_2_q31[2]), .d30(out_8[1]),
    .q30(shift_register_2_q31[1]), .d31(out_8[0]), .q31(shift_register_2_q31[0]));  // open: in, out, clr
  Shift_Register #(.length(32), .trigger("falling")) shift_register_3 (
    .shift(counter_1_carry), .clk(\и ), .load(comparator_1_eq), .d0(out_8[31]), .q0(shift_register_3_q0[0]),
    .d1(out_8[30]), .q1(shift_register_3_q0[1]), .d2(out_8[29]), .q2(shift_register_3_q0[2]), .d3(out_8[28]),
    .q3(shift_register_3_q0[3]), .d4(out_8[27]), .q4(shift_register_3_q0[4]), .d5(out_8[26]),
    .q5(shift_register_3_q0[5]), .d6(out_8[25]), .q6(shift_register_3_q0[6]), .d7(out_8[24]),
    .q7(shift_register_3_q0[7]), .d8(out_8[23]), .q8(shift_register_3_q0[8]), .d9(out_8[22]),
    .q9(shift_register_3_q0[9]), .d10(out_8[21]), .q10(shift_register_3_q0[10]), .d11(out_8[20]),
    .q11(shift_register_3_q0[11]), .d12(out_8[19]), .q12(shift_register_3_q0[12]), .d13(out_8[18]),
    .q13(shift_register_3_q0[13]), .d14(out_8[17]), .q14(shift_register_3_q0[14]), .d15(out_8[16]),
    .q15(shift_register_3_q0[15]), .d16(out_8[15]), .q16(shift_register_3_q0[16]), .d17(out_8[14]),
    .q17(shift_register_3_q0[17]), .d18(out_8[13]), .q18(shift_register_3_q0[18]), .d19(out_8[12]),
    .q19(shift_register_3_q0[19]), .d20(out_8[11]), .q20(shift_register_3_q0[20]), .d21(out_8[10]),
    .q21(shift_register_3_q0[21]), .d22(out_8[9]), .q22(shift_register_3_q0[22]), .d23(out_8[8]),
    .q23(shift_register_3_q0[23]), .d24(out_8[7]), .q24(shift_register_3_q0[24]), .d25(out_8[6]),
    .q25(shift_register_3_q0[25]), .d26(out_8[5]), .q26(shift_register_3_q0[26]), .d27(out_8[4]),
    .q27(shift_register_3_q0[27]), .d28(out_8[3]), .q28(shift_register_3_q0[28]), .d29(out_8[2]),
    .q29(shift_register_3_q0[29]), .d30(out_8[1]), .q30(shift_register_3_q0[30]), .d31(out_8[0]),
    .q31(shift_register_3_q0[31]));  // open: in, out, clr
  DotMatrix #(.inputtype("row"), .matrixcols(32), .matrixrows(32)) dotmatrix_1 (
    .row0(shift_register_1_q0), .row1(shift_register_1_q1), .row2(shift_register_1_q2),
    .row3(shift_register_1_q3), .row4(shift_register_1_q4), .row5(shift_register_1_q5),
    .row6(shift_register_1_q6));  // open: row7, row8, row9, row10, row11, row12, row13, row14, row15, row16, row17, row18, row19, row20, row21, row22, row23, row24, row25, row26, row27, row28, row29, row30, row31
  not not_1 (not_1_out, and_1_out);
  assign pull_resistor_1_node = and_1_out ? shift_register_2_q31 : 32'bz;  // Controlled_Buffer controlled_buffer_1
  assign pull_resistor_1_node = not_1_out ? shift_register_3_q0 : 32'bz;  // Controlled_Buffer controlled_buffer_2
endmodule

module \miniReg__не_используется  (
  input  [31:0] inp1,
  input  clock,
  input  in_3,
  input  [31:0] inp0,
  output [31:0] out
);

  wire not_1_out;
  wire [31:0] controlled_buffer_1_out;

  assign controlled_buffer_1_out = in_3 ? inp1 : 32'bz;  // Controlled_Buffer controlled_buffer_1
  not not_1 (not_1_out, in_3);
  assign controlled_buffer_1_out = not_1_out ? inp0 : 32'bz;  // Controlled_Buffer controlled_buffer_2
  Register #(.width(32)) register_1 (.D(controlled_buffer_1_out), .Q(out), .clk(clock));  // open: en, clr
endmodule

module shifterDown (
  input  [31:0] \Вход_0 ,
  input  [31:0] in_2,
  input  [3:0] in_3,
  input  [31:0] in_4,
  input  En,
  input  [31:0] in_6,
  input  [31:0] in_7,
  input  [31:0] in_8,
  input  [31:0] in_9,
  input  [31:0] in_10,
  input  [31:0] in_11,
  input  [31:0] in_12,
  input  [31:0] in_13,
  input  [31:0] in_14,
  input  [31:0] in_15,
  input  [31:0] in_16,
  input  [31:0] in_17,
  input  [31:0] in_18,
  output [31:0] \Выход_0 ,
  output [31:0] out_20,
  output [31:0] out_21,
  output [31:0] out_22,
  output [31:0] out_23,
  output [31:0] out_24,
  output [31:0] out_25,
  output [31:0] out_26,
  output [31:0] out_27,
  output [31:0] out_28,
  output [31:0] out_29,
  output [31:0] out_30,
  output [31:0] out_31,
  output [31:0] out_32,
  output [31:0] out_33,
  output [31:0] out_34
);

  wire not_1_out;
  wire [3:0] controlled_buffer_1_out, dec4_1_r, dec4_2_r, dec4_3_r, dec4_4_r, dec4_5_r, dec4_6_r, dec4_7_r,
       dec4_8_r, dec4_9_r, dec4_10_r, dec4_11_r, dec4_12_r, dec4_13_r, dec4_14_r, dec4_15_r;
  wire [31:0] demultiplexer_1_out0, demultiplexer_1_out1, demultiplexer_1_out2, demultiplexer_1_out3,
       demultiplexer_1_out4, demultiplexer_1_out5, demultiplexer_1_out6, demultiplexer_1_out7,
       demultiplexer_1_out8, demultiplexer_1_out9, demultiplexer_1_out10, demultiplexer_1_out11,
       demultiplexer_1_out12, demultiplexer_1_out13, demultiplexer_1_out14, demultiplexer_1_out15,
       demultiplexer_2_out4, demultiplexer_2_out5, demultiplexer_2_out6, demultiplexer_2_out7,
       demultiplexer_2_out8, demultiplexer_2_out9, demultiplexer_2_out10, demultiplexer_2_out11,
       demultiplexer_2_out12, demultiplexer_2_out13, demultiplexer_2_out14, demultiplexer_2_out15,
       demultiplexer_3_out8, demultiplexer_3_out9, demultiplexer_3_out10, demultiplexer_3_out11,
       demultiplexer_3_out12, demultiplexer_3_out13, demultiplexer_3_out14, demultiplexer_3_out15,
       demultiplexer_4_out12, demultiplexer_4_out13, demultiplexer_4_out14, demultiplexer_4_out15,
       demultiplexer_5_out1, demultiplexer_5_out2, demultiplexer_5_out3, demultiplexer_5_out4,
       demultiplexer_5_out5, demultiplexer_5_out6, demultiplexer_5_out7, demultiplexer_5_out8,
       demultiplexer_5_out9, demultiplexer_5_out10, demultiplexer_5_out11, demultiplexer_5_out12,
       demultiplexer_5_out13, demultiplexer_5_out14, demultiplexer_5_out15, demultiplexer_6_out5,
       demultiplexer_6_out6, demultiplexer_6_out7, demultiplexer_6_out8, demultiplexer_6_out9,
       demultiplexer_6_out10, demultiplexer_6_out11, demultiplexer_6_out12, demultiplexer_6_out13,
       demultiplexer_6_out14, demultiplexer_6_out15, demultiplexer_7_out9, demultiplexer_7_out10,
       demultiplexer_7_out11, demultiplexer_7_out12, demultiplexer_7_out13, demultiplexer_7_out14,
       demultiplexer_7_out15, demultiplexer_8_out13, demultiplexer_8_out14, demultiplexer_8_out15,
       demultiplexer_9_out2, demultiplexer_9_out3, demultiplexer_9_out4, demultiplexer_9_out5,
       demultiplexer_9_out6, demultiplexer_9_out7, demultiplexer_9_out8, demultiplexer_9_out9,
       demultiplexer_9_out10, demultiplexer_9_out11, demultiplexer_9_out12, demultiplexer_9_out13,
       demultiplexer_9_out14, demultiplexer_9_out15, demultiplexer_10_out6, demultiplexer_10_out7,
       demultiplexer_10_out8, demultiplexer_10_out9, demultiplexer_10_out10, demultiplexer_10_out11,
       demultiplexer_10_out12, demultiplexer_10_out13, demultiplexer_10_out14, demultiplexer_10_out15,
       demultiplexer_11_out10, demultiplexer_11_out11, demultiplexer_11_out12, demultiplexer_11_out13,
       demultiplexer_11_out14, demultiplexer_11_out15, demultiplexer_12_out14, demultiplexer_12_out15,
       demultiplexer_13_out3, demultiplexer_13_out4, demultiplexer_13_out5, demultiplexer_13_out6,
       demultiplexer_13_out7, demultiplexer_13_out8, demultiplexer_13_out9, demultiplexer_13_out10,
       demultiplexer_13_out11, demultiplexer_13_out12, demultiplexer_13_out13, demultiplexer_13_out14,
       demultiplexer_13_out15, demultiplexer_14_out7, demultiplexer_14_out8, demultiplexer_14_out9,
       demultiplexer_14_out10, demultiplexer_14_out11, demultiplexer_14_out12, demultiplexer_14_out13,
       demultiplexer_14_out14, demultiplexer_14_out15, demultiplexer_15_out11, demultiplexer_15_out12,
       demultiplexer_15_out13, demultiplexer_15_out14, demultiplexer_15_out15, demultiplexer_16_out15;

  Pull_Resistor pull_resistor_1 (.node(\Выход_0 ));
  Pull_Resistor pull_resistor_2 (.node(out_20));
  Pull_Resistor pull_resistor_3 (.node(out_21));
  Pull_Resistor pull_resistor_4 (.node(out_22));
  Pull_Resistor pull_resistor_5 (.node(out_23));
  Pull_Resistor pull_resistor_6 (.node(out_24));
  Pull_Resistor pull_resistor_7 (.node(out_25));
  Pull_Resistor pull_resistor_8 (.node(out_26));
  Pull_Resistor pull_resistor_9 (.node(out_27));
  Pull_Resistor pull_resistor_10 (.node(out_28));
  Pull_Resistor pull_resistor_11 (.node(out_29));
  Pull_Resistor pull_resistor_12 (.node(out_30));
  Pull_Resistor pull_resistor_13 (.node(out_31));
  Pull_Resistor pull_resistor_14 (.node(out_32));
  Pull_Resistor pull_resistor_15 (.node(out_33));
  Pull_Resistor pull_resistor_16 (.node(out_34));
  assign controlled_buffer_1_out = En ? in_3 : 4'bz;  // Controlled_Buffer controlled_buffer_1
  not not_1 (not_1_out, En);
  assign controlled_buffer_1_out = not_1_out ? 4'b0000 : 4'bz;  // Controlled_Buffer controlled_buffer_2
  Demultiplexer #(.select(4), .width(32)) demultiplexer_1 (
    .out0(demultiplexer_1_out0), .out1(demultiplexer_1_out1), .out2(demultiplexer_1_out2),
    .out3(demultiplexer_1_out3), .out4(demultiplexer_1_out4), .out5(demultiplexer_1_out5),
    .out6(demultiplexer_1_out6), .out7(demultiplexer_1_out7), .out8(demultiplexer_1_out8),
    .out9(demultiplexer_1_out9), .out10(demultiplexer_1_out10), .out11(demultiplexer_1_out11),
    .out12(demultiplexer_1_out12), .out13(demultiplexer_1_out13), .out14(demultiplexer_1_out14),
    .out15(demultiplexer_1_out15), .in(\Вход_0 ), .sel(controlled_buffer_1_out));  // open: en
  Demultiplexer #(.select(4), .width(32)) demultiplexer_2 (
    .out4(demultiplexer_2_out4), .out5(demultiplexer_2_out5), .out6(demultiplexer_2_out6),
    .out7(demultiplexer_2_out7), .out8(demultiplexer_2_out8), .out9(demultiplexer_2_out9),
    .out10(demultiplexer_2_out10), .out11(demultiplexer_2_out11), .out12(demultiplexer_2_out12),
    .out13(demultiplexer_2_out13), .out14(demultiplexer_2_out14), .out15(demultiplexer_2_out15), .in(in_7),
    .sel(dec4_1_r));  // open: out0, out1, out2, out3, en
  dec4 dec4_1 (.X(dec4_12_r), .R(dec4_1_r));  // open: Cout
  Demultiplexer #(.select(4), .width(32)) demultiplexer_3 (
    .out8(demultiplexer_3_out8), .out9(demultiplexer_3_out9), .out10(demultiplexer_3_out10),
    .out11(demultiplexer_3_out11), .out12(demultiplexer_3_out12), .out13(demultiplexer_3_out13),
    .out14(demultiplexer_3_out14), .out15(demultiplexer_3_out15), .in(in_11), .sel(dec4_2_r));  // open: out0, out1, out2, out3, out4, out5, out6, out7, en
  dec4 dec4_2 (.X(dec4_13_r), .R(dec4_2_r));  // open: Cout
  Demultiplexer #(.select(4), .width(32)) demultiplexer_4 (
    .out12(demultiplexer_4_out12), .out13(demultiplexer_4_out13), .out14(demultiplexer_4_out14),
    .out15(demultiplexer_4_out15), .in(in_15), .sel(dec4_3_r));  // open: out0, out1, out2, out3, out4, out5, out6, out7, out8, out9, out10, out11, en
  dec4 dec4_3 (.X(dec4_14_r), .R(dec4_3_r));  // open: Cout
  decodBufer decodbufer_1 (.in_1(demultiplexer_1_out0), .out_2(\Выход_0 ));
  decodBufer decodbufer_2 (.in_1(demultiplexer_1_out1), .out_2(out_20));
  decodBufer decodbufer_3 (.in_1(demultiplexer_1_out2), .out_2(out_21));
  decodBufer decodbufer_4 (.in_1(demultiplexer_1_out3), .out_2(out_22));
  decodBufer decodbufer_5 (.in_1(demultiplexer_1_out4), .out_2(out_23));
  decodBufer decodbufer_6 (.in_1(demultiplexer_1_out5), .out_2(out_24));
  decodBufer decodbufer_7 (.in_1(demultiplexer_1_out6), .out_2(out_25));
  decodBufer decodbufer_8 (.in_1(demultiplexer_1_out7), .out_2(out_26));
  decodBufer decodbufer_9 (.in_1(demultiplexer_1_out8), .out_2(out_27));
  decodBufer decodbufer_10 (.in_1(demultiplexer_1_out9), .out_2(out_28));
  decodBufer decodbufer_11 (.in_1(demultiplexer_1_out10), .out_2(out_29));
  decodBufer decodbufer_12 (.in_1(demultiplexer_1_out11), .out_2(out_30));
  decodBufer decodbufer_13 (.in_1(demultiplexer_1_out12), .out_2(out_31));
  decodBufer decodbufer_14 (.in_1(demultiplexer_1_out13), .out_2(out_32));
  decodBufer decodbufer_15 (.in_1(demultiplexer_1_out14), .out_2(out_33));
  decodBufer decodbufer_16 (.in_1(demultiplexer_1_out15), .out_2(out_34));
  dec4 dec4_4 (.X(controlled_buffer_1_out), .R(dec4_4_r));  // open: Cout
  decodBufer decodbufer_17 (.in_1(demultiplexer_2_out4), .out_2(out_23));
  decodBufer decodbufer_18 (.in_1(demultiplexer_2_out5), .out_2(out_24));
  decodBufer decodbufer_19 (.in_1(demultiplexer_2_out6), .out_2(out_25));
  decodBufer decodbufer_20 (.in_1(demultiplexer_2_out7), .out_2(out_26));
  decodBufer decodbufer_21 (.in_1(demultiplexer_2_out8), .out_2(out_27));
  decodBufer decodbufer_22 (.in_1(demultiplexer_2_out9), .out_2(out_28));
  decodBufer decodbufer_23 (.in_1(demultiplexer_2_out10), .out_2(out_29));
  decodBufer decodbufer_24 (.in_1(demultiplexer_2_out11), .out_2(out_30));
  decodBufer decodbufer_25 (.in_1(demultiplexer_2_out12), .out_2(out_31));
  decodBufer decodbufer_26 (.in_1(demultiplexer_2_out13), .out_2(out_32));
  decodBufer decodbufer_27 (.in_1(demultiplexer_2_out14), .out_2(out_33));
  decodBufer decodbufer_28 (.in_1(demultiplexer_2_out15), .out_2(out_34));
  dec4 dec4_5 (.X(dec4_1_r), .R(dec4_5_r));  // open: Cout
  decodBufer decodbufer_29 (.in_1(demultiplexer_3_out8), .out_2(out_27));
  decodBufer decodbufer_30 (.in_1(demultiplexer_3_out9), .out_2(out_28));
  decodBufer decodbufer_31 (.in_1(demultiplexer_3_out10), .out_2(out_29));
  decodBufer decodbufer_32 (.in_1(demultiplexer_3_out11), .out_2(out_30));
  decodBufer decodbufer_33 (.in_1(demultiplexer_3_out12), .out_2(out_31));
  decodBufer decodbufer_34 (.in_1(demultiplexer_3_out13), .out_2(out_32));
  decodBufer decodbufer_35 (.in_1(demultiplexer_3_out14), .out_2(out_33));
  decodBufer decodbufer_36 (.in_1(demultiplexer_3_out15), .out_2(out_34));
  dec4 dec4_6 (.X(dec4_2_r), .R(dec4_6_r));  // open: Cout
  decodBufer decodbufer_37 (.in_1(demultiplexer_4_out12), .out_2(out_31));
  decodBufer decodbufer_38 (.in_1(demultiplexer_4_out13), .out_2(out_32));
  decodBufer decodbufer_39 (.in_1(demultiplexer_4_out14), .out_2(out_33));
  decodBufer decodbufer_40 (.in_1(demultiplexer_4_out15), .out_2(out_34));
  dec4 dec4_7 (.X(dec4_3_r), .R(dec4_7_r));  // open: Cout
  Demultiplexer #(.select(4), .width(32)) demultiplexer_5 (
    .out1(demultiplexer_5_out1), .out2(demultiplexer_5_out2), .out3(demultiplexer_5_out3),
    .out4(demultiplexer_5_out4), .out5(demultiplexer_5_out5), .out6(demultiplexer_5_out6),
    .out7(demultiplexer_5_out7), .out8(demultiplexer_5_out8), .out9(demultiplexer_5_out9),
    .out10(demultiplexer_5_out10), .out11(demultiplexer_5_out11), .out12(demultiplexer_5_out12),
    .out13(demultiplexer_5_out13), .out14(demultiplexer_5_out14), .out15(demultiplexer_5_out15), .in(in_2),
    .sel(dec4_4_r));  // open: out0, en
  Demultiplexer #(.select(4), .width(32)) demultiplexer_6 (
    .out5(demultiplexer_6_out5), .out6(demultiplexer_6_out6), .out7(demultiplexer_6_out7),
    .out8(demultiplexer_6_out8), .out9(demultiplexer_6_out9), .out10(demultiplexer_6_out10),
    .out11(demultiplexer_6_out11), .out12(demultiplexer_6_out12), .out13(demultiplexer_6_out13),
    .out14(demultiplexer_6_out14), .out15(demultiplexer_6_out15), .in(in_8), .sel(dec4_5_r));  // open: out0, out1, out2, out3, out4, en
  Demultiplexer #(.select(4), .width(32)) demultiplexer_7 (
    .out9(demultiplexer_7_out9), .out10(demultiplexer_7_out10), .out11(demultiplexer_7_out11),
    .out12(demultiplexer_7_out12), .out13(demultiplexer_7_out13), .out14(demultiplexer_7_out14),
    .out15(demultiplexer_7_out15), .in(in_12), .sel(dec4_6_r));  // open: out0, out1, out2, out3, out4, out5, out6, out7, out8, en
  Demultiplexer #(.select(4), .width(32)) demultiplexer_8 (
    .out13(demultiplexer_8_out13), .out14(demultiplexer_8_out14), .out15(demultiplexer_8_out15), .in(in_16),
    .sel(dec4_7_r));  // open: out0, out1, out2, out3, out4, out5, out6, out7, out8, out9, out10, out11, out12, en
  decodBufer decodbufer_41 (.in_1(demultiplexer_5_out1), .out_2(out_20));
  decodBufer decodbufer_42 (.in_1(demultiplexer_5_out2), .out_2(out_21));
  decodBufer decodbufer_43 (.in_1(demultiplexer_5_out3), .out_2(out_22));
  decodBufer decodbufer_44 (.in_1(demultiplexer_5_out4), .out_2(out_23));
  decodBufer decodbufer_45 (.in_1(demultiplexer_5_out5), .out_2(out_24));
  decodBufer decodbufer_46 (.in_1(demultiplexer_5_out6), .out_2(out_25));
  decodBufer decodbufer_47 (.in_1(demultiplexer_5_out7), .out_2(out_26));
  decodBufer decodbufer_48 (.in_1(demultiplexer_5_out8), .out_2(out_27));
  Demultiplexer #(.select(4), .width(32)) demultiplexer_9 (
    .out2(demultiplexer_9_out2), .out3(demultiplexer_9_out3), .out4(demultiplexer_9_out4),
    .out5(demultiplexer_9_out5), .out6(demultiplexer_9_out6), .out7(demultiplexer_9_out7),
    .out8(demultiplexer_9_out8), .out9(demultiplexer_9_out9), .out10(demultiplexer_9_out10),
    .out11(demultiplexer_9_out11), .out12(demultiplexer_9_out12), .out13(demultiplexer_9_out13),
    .out14(demultiplexer_9_out14), .out15(demultiplexer_9_out15), .in(in_4), .sel(dec4_8_r));  // open: out0, out1, en
  decodBufer decodbufer_49 (.in_1(demultiplexer_5_out9), .out_2(out_28));
  decodBufer decodbufer_50 (.in_1(demultiplexer_5_out10), .out_2(out_29));
  decodBufer decodbufer_51 (.in_1(demultiplexer_5_out11), .out_2(out_30));
  decodBufer decodbufer_52 (.in_1(demultiplexer_5_out12), .out_2(out_31));
  decodBufer decodbufer_53 (.in_1(demultiplexer_5_out13), .out_2(out_32));
  decodBufer decodbufer_54 (.in_1(demultiplexer_5_out14), .out_2(out_33));
  decodBufer decodbufer_55 (.in_1(demultiplexer_5_out15), .out_2(out_34));
  dec4 dec4_8 (.X(dec4_4_r), .R(dec4_8_r));  // open: Cout
  decodBufer decodbufer_56 (.in_1(demultiplexer_6_out5), .out_2(out_24));
  decodBufer decodbufer_57 (.in_1(demultiplexer_6_out6), .out_2(out_25));
  decodBufer decodbufer_58 (.in_1(demultiplexer_6_out7), .out_2(out_26));
  decodBufer decodbufer_59 (.in_1(demultiplexer_6_out8), .out_2(out_27));
  Demultiplexer #(.select(4), .width(32)) demultiplexer_10 (
    .out6(demultiplexer_10_out6), .out7(demultiplexer_10_out7), .out8(demultiplexer_10_out8),
    .out9(demultiplexer_10_out9), .out10(demultiplexer_10_out10), .out11(demultiplexer_10_out11),
    .out12(demultiplexer_10_out12), .out13(demultiplexer_10_out13), .out14(demultiplexer_10_out14),
    .out15(demultiplexer_10_out15), .in(in_9), .sel(dec4_9_r));  // open: out0, out1, out2, out3, out4, out5, en
  decodBufer decodbufer_60 (.in_1(demultiplexer_6_out9), .out_2(out_28));
  decodBufer decodbufer_61 (.in_1(demultiplexer_6_out10), .out_2(out_29));
  decodBufer decodbufer_62 (.in_1(demultiplexer_6_out11), .out_2(out_30));
  decodBufer decodbufer_63 (.in_1(demultiplexer_6_out12), .out_2(out_31));
  decodBufer decodbufer_64 (.in_1(demultiplexer_6_out13), .out_2(out_32));
  decodBufer decodbufer_65 (.in_1(demultiplexer_6_out14), .out_2(out_33));
  decodBufer decodbufer_66 (.in_1(demultiplexer_6_out15), .out_2(out_34));
  dec4 dec4_9 (.X(dec4_5_r), .R(dec4_9_r));  // open: Cout
  Demultiplexer #(.select(4), .width(32)) demultiplexer_11 (
    .out10(demultiplexer_11_out10), .out11(demultiplexer_11_out11), .out12(demultiplexer_11_out12),
    .out13(demultiplexer_11_out13), .out14(demultiplexer_11_out14), .out15(demultiplexer_11_out15),
    .in(in_13), .sel(dec4_10_r));  // open: out0, out1, out2, out3, out4, out5, out6, out7, out8, out9, en
  decodBufer decodbufer_67 (.in_1(demultiplexer_7_out9), .out_2(out_28));
  decodBufer decodbufer_68 (.in_1(demultiplexer_7_out10), .out_2(out_29));
  decodBufer decodbufer_69 (.in_1(demultiplexer_7_out11), .out_2(out_30));
  decodBufer decodbufer_70 (.in_1(demultiplexer_7_out12), .out_2(out_31));
  decodBufer decodbufer_71 (.in_1(demultiplexer_7_out13), .out_2(out_32));
  decodBufer decodbufer_72 (.in_1(demultiplexer_7_out14), .out_2(out_33));
  decodBufer decodbufer_73 (.in_1(demultiplexer_7_out15), .out_2(out_34));
  dec4 dec4_10 (.X(dec4_6_r), .R(dec4_10_r));  // open: Cout
  Demultiplexer #(.select(4), .width(32)) demultiplexer_12 (
    .out14(demultiplexer_12_out14), .out15(demultiplexer_12_out15), .in(in_17), .sel(dec4_11_r));  // open: out0, out1, out2, out3, out4, out5, out6, out7, out8, out9, out10, out11, out12, out13, en
  decodBufer decodbufer_74 (.in_1(demultiplexer_8_out13), .out_2(out_32));
  decodBufer decodbufer_75 (.in_1(demultiplexer_8_out14), .out_2(out_33));
  decodBufer decodbufer_76 (.in_1(demultiplexer_8_out15), .out_2(out_34));
  dec4 dec4_11 (.X(dec4_7_r), .R(dec4_11_r));  // open: Cout
  decodBufer decodbufer_77 (.in_1(demultiplexer_9_out2), .out_2(out_21));
  decodBufer decodbufer_78 (.in_1(demultiplexer_9_out3), .out_2(out_22));
  decodBufer decodbufer_79 (.in_1(demultiplexer_9_out4), .out_2(out_23));
  decodBufer decodbufer_80 (.in_1(demultiplexer_9_out5), .out_2(out_24));
  decodBufer decodbufer_81 (.in_1(demultiplexer_9_out6), .out_2(out_25));
  decodBufer decodbufer_82 (.in_1(demultiplexer_9_out7), .out_2(out_26));
  decodBufer decodbufer_83 (.in_1(demultiplexer_9_out8), .out_2(out_27));
  decodBufer decodbufer_84 (.in_1(demultiplexer_9_out9), .out_2(out_28));
  decodBufer decodbufer_85 (.in_1(demultiplexer_9_out10), .out_2(out_29));
  decodBufer decodbufer_86 (.in_1(demultiplexer_9_out11), .out_2(out_30));
  decodBufer decodbufer_87 (.in_1(demultiplexer_9_out12), .out_2(out_31));
  decodBufer decodbufer_88 (.in_1(demultiplexer_9_out13), .out_2(out_32));
  decodBufer decodbufer_89 (.in_1(demultiplexer_9_out14), .out_2(out_33));
  decodBufer decodbufer_90 (.in_1(demultiplexer_9_out15), .out_2(out_34));
  decodBufer decodbufer_91 (.in_1(demultiplexer_10_out6), .out_2(out_25));
  decodBufer decodbufer_92 (.in_1(demultiplexer_10_out7), .out_2(out_26));
  decodBufer decodbufer_93 (.in_1(demultiplexer_10_out8), .out_2(out_27));
  decodBufer decodbufer_94 (.in_1(demultiplexer_10_out9), .out_2(out_28));
  decodBufer decodbufer_95 (.in_1(demultiplexer_10_out10), .out_2(out_29));
  decodBufer decodbufer_96 (.in_1(demultiplexer_10_out11), .out_2(out_30));
  decodBufer decodbufer_97 (.in_1(demultiplexer_10_out12), .out_2(out_31));
  decodBufer decodbufer_98 (.in_1(demultiplexer_10_out13), .out_2(out_32));
  decodBufer decodbufer_99 (.in_1(demultiplexer_10_out14), .out_2(out_33));
  decodBufer decodbufer_100 (.in_1(demultiplexer_10_out15), .out_2(out_34));
  decodBufer decodbufer_101 (.in_1(demultiplexer_11_out10), .out_2(out_29));
  decodBufer decodbufer_102 (.in_1(demultiplexer_11_out11), .out_2(out_30));
  decodBufer decodbufer_103 (.in_1(demultiplexer_11_out12), .out_2(out_31));
  decodBufer decodbufer_104 (.in_1(demultiplexer_11_out13), .out_2(out_32));
  decodBufer decodbufer_105 (.in_1(demultiplexer_11_out14), .out_2(out_33));
  decodBufer decodbufer_106 (.in_1(demultiplexer_11_out15), .out_2(out_34));
  decodBufer decodbufer_107 (.in_1(demultiplexer_12_out14), .out_2(out_33));
  decodBufer decodbufer_108 (.in_1(demultiplexer_12_out15), .out_2(out_34));
  Demultiplexer #(.select(4), .width(32)) demultiplexer_13 (
    .out3(demultiplexer_13_out3), .out4(demultiplexer_13_out4), .out5(demultiplexer_13_out5),
    .out6(demultiplexer_13_out6), .out7(demultiplexer_13_out7), .out8(demultiplexer_13_out8),
    .out9(demultiplexer_13_out9), .out10(demultiplexer_13_out10), .out11(demultiplexer_13_out11),
    .out12(demultiplexer_13_out12), .out13(demultiplexer_13_out13), .out14(demultiplexer_13_out14),
    .out15(demultiplexer_13_out15), .in(in_6), .sel(dec4_12_r));  // open: out0, out1, out2, en
  dec4 dec4_12 (.X(dec4_8_r), .R(dec4_12_r));  // open: Cout
  Demultiplexer #(.select(4), .width(32)) demultiplexer_14 (
    .out7(demultiplexer_14_out7), .out8(demultiplexer_14_out8), .out9(demultiplexer_14_out9),
    .out10(demultiplexer_14_out10), .out11(demultiplexer_14_out11), .out12(demultiplexer_14_out12),
    .out13(demultiplexer_14_out13), .out14(demultiplexer_14_out14), .out15(demultiplexer_14_out15),
    .in(in_10), .sel(dec4_13_r));  // open: out0, out1, out2, out3, out4, out5, out6, en
  dec4 dec4_13 (.X(dec4_9_r), .R(dec4_13_r));  // open: Cout
  Demultiplexer #(.select(4), .width(32)) demultiplexer_15 (
    .out11(demultiplexer_15_out11), .out12(demultiplexer_15_out12), .out13(demultiplexer_15_out13),
    .out14(demultiplexer_15_out14), .out15(demultiplexer_15_out15), .in(in_14), .sel(dec4_14_r));  // open: out0, out1, out2, out3, out4, out5, out6, out7, out8, out9, out10, en
  dec4 dec4_14 (.X(dec4_10_r), .R(dec4_14_r));  // open: Cout
  Demultiplexer #(.select(4), .width(32)) demultiplexer_16 (
    .out15(demultiplexer_16_out15), .in(in_18), .sel(dec4_15_r));  // open: out0, out1, out2, out3, out4, out5, out6, out7, out8, out9, out10, out11, out12, out13, out14, en
  dec4 dec4_15 (.X(dec4_11_r), .R(dec4_15_r));  // open: Cout
  decodBufer decodbufer_109 (.in_1(demultiplexer_13_out3), .out_2(out_22));
  decodBufer decodbufer_110 (.in_1(demultiplexer_13_out4), .out_2(out_23));
  decodBufer decodbufer_111 (.in_1(demultiplexer_13_out5), .out_2(out_24));
  decodBufer decodbufer_112 (.in_1(demultiplexer_13_out6), .out_2(out_25));
  decodBufer decodbufer_113 (.in_1(demultiplexer_13_out7), .out_2(out_26));
  decodBufer decodbufer_114 (.in_1(demultiplexer_13_out8), .out_2(out_27));
  decodBufer decodbufer_115 (.in_1(demultiplexer_13_out9), .out_2(out_28));
  decodBufer decodbufer_116 (.in_1(demultiplexer_13_out10), .out_2(out_29));
  decodBufer decodbufer_117 (.in_1(demultiplexer_13_out11), .out_2(out_30));
  decodBufer decodbufer_118 (.in_1(demultiplexer_13_out12), .out_2(out_31));
  decodBufer decodbufer_119 (.in_1(demultiplexer_13_out13), .out_2(out_32));
  decodBufer decodbufer_120 (.in_1(demultiplexer_13_out14), .out_2(out_33));
  decodBufer decodbufer_121 (.in_1(demultiplexer_13_out15), .out_2(out_34));
  decodBufer decodbufer_122 (.in_1(demultiplexer_14_out7), .out_2(out_26));
  decodBufer decodbufer_123 (.in_1(demultiplexer_14_out8), .out_2(out_27));
  decodBufer decodbufer_124 (.in_1(demultiplexer_14_out9), .out_2(out_28));
  decodBufer decodbufer_125 (.in_1(demultiplexer_14_out10), .out_2(out_29));
  decodBufer decodbufer_126 (.in_1(demultiplexer_14_out11), .out_2(out_30));
  decodBufer decodbufer_127 (.in_1(demultiplexer_14_out12), .out_2(out_31));
  decodBufer decodbufer_128 (.in_1(demultiplexer_14_out13), .out_2(out_32));
  decodBufer decodbufer_129 (.in_1(demultiplexer_14_out14), .out_2(out_33));
  decodBufer decodbufer_130 (.in_1(demultiplexer_14_out15), .out_2(out_34));
  decodBufer decodbufer_131 (.in_1(demultiplexer_15_out11), .out_2(out_30));
  decodBufer decodbufer_132 (.in_1(demultiplexer_15_out12), .out_2(out_31));
  decodBufer decodbufer_133 (.in_1(demultiplexer_15_out13), .out_2(out_32));
  decodBufer decodbufer_134 (.in_1(demultiplexer_15_out14), .out_2(out_33));
  decodBufer decodbufer_135 (.in_1(demultiplexer_15_out15), .out_2(out_34));
  decodBufer decodbufer_136 (.in_1(demultiplexer_16_out15), .out_2(out_34));

  // Other names for the same wires on the sheet: _0[31:0] = \Вход_0 ; _0_prime[31:0] = \Выход_0 ; _1[31:0] = in_2;
  //   _1_prime[31:0] = out_20; _2[31:0] = in_4; _2_prime[31:0] = out_21; _3[31:0] = in_6; _3_prime[31:0] = out_22;
  //   _4[31:0] = in_7; _4_prime[31:0] = out_23; _5[31:0] = in_8; _5_prime[31:0] = out_24; _6[31:0] = in_9;
  //   _6_prime[31:0] = out_25; _7[31:0] = in_10; _7_prime[31:0] = out_26; _8[31:0] = in_11; _8_prime[31:0] = out_27;
  //   _9[31:0] = in_12; _9_prime[31:0] = out_28; _10[31:0] = in_13; _10_prime[31:0] = out_29; _11[31:0] = in_14;
  //   _11_prime[31:0] = out_30; _12[31:0] = in_15; _12_prime[31:0] = out_31; _13[31:0] = in_16;
  //   _13_prime[31:0] = out_32; _14[31:0] = in_17; _14_prime[31:0] = out_33; _15[31:0] = in_18;
  //   _15_prime[31:0] = out_34
endmodule

module decodBufer (
  input  [31:0] in_1,
  output [31:0] out_2
);

  wire oradd32_1_out;

  oradd32 oradd32_1 (.in(in_1), .out(oradd32_1_out));
  assign out_2 = oradd32_1_out ? in_1 : 32'bz;  // Controlled_Buffer controlled_buffer_1

  // Notes on the sheet:
  //   out_2: pull=down
endmodule

module dec4 (
  input  [3:0] X,
  output [3:0] R,
  output Cout
);

  wire [2:0] and_1_out;

  assign {Cout, and_1_out} = {and_1_out, 1'b1} & X;  // AND_Gate and_1, 4 bits wide
  assign R = X ^ {and_1_out, 1'b1};  // XOR_Gate xor_1, 4 bits wide
endmodule

module ShifterLeft (
  input  [31:0] \Вход_0 ,
  input  [31:0] in_2,
  input  [31:0] in_3,
  input  [31:0] in_4,
  input  [31:0] in_5,
  input  [31:0] in_6,
  input  [31:0] in_7,
  input  [31:0] in_8,
  input  [31:0] in_9,
  input  [31:0] in_10,
  input  [31:0] in_11,
  input  [31:0] in_12,
  input  [31:0] in_13,
  input  [31:0] in_14,
  input  [31:0] in_15,
  input  [31:0] in_16,
  input  in_17,
  output [31:0] out_18,
  output [31:0] out_19,
  output [31:0] out_20,
  output [31:0] out_21,
  output [31:0] out_22,
  output [31:0] out_23,
  output [31:0] out_24,
  output [31:0] out_25,
  output [31:0] out_26,
  output [31:0] out_27,
  output [31:0] out_28,
  output [31:0] out_29,
  output [31:0] out_30,
  output [31:0] out_31,
  output [31:0] out_32,
  output [31:0] out_33
);

  wire [4:4] pull_resistor_1_node;
  wire [31:0] pull_resistor_8_node, pull_resistor_9_node, pull_resistor_10_node, pull_resistor_11_node,
       pull_resistor_12_node, pull_resistor_14_node, pull_resistor_15_node, shifter_1_out, shifter_2_out,
       shifter_3_out, shifter_4_out, shifter_5_out, shifter_6_out, shifter_12_out, shifter_15_out,
       shifter_16_out;

  Pull_Resistor pull_resistor_1 (.node(pull_resistor_1_node[4]));
  Shifter #(.width(32)) shifter_1 (.in(\Вход_0 ), .\dist ({{4{pull_resistor_1_node[4]}}, in_17}), .out(shifter_1_out));
  Pull_Resistor pull_resistor_2 (.node(shifter_1_out));
  Shifter #(.width(32)) shifter_2 (.in(in_2), .\dist ({{4{pull_resistor_1_node[4]}}, in_17}), .out(shifter_2_out));
  Pull_Resistor pull_resistor_3 (.node(shifter_2_out));
  Shifter #(.width(32)) shifter_3 (.in(in_3), .\dist ({{4{pull_resistor_1_node[4]}}, in_17}), .out(shifter_3_out));
  Pull_Resistor pull_resistor_4 (.node(shifter_3_out));
  Shifter #(.width(32)) shifter_4 (.in(in_4), .\dist ({{4{pull_resistor_1_node[4]}}, in_17}), .out(shifter_4_out));
  Pull_Resistor pull_resistor_5 (.node(shifter_4_out));
  Shifter #(.width(32)) shifter_5 (.in(in_5), .\dist ({{4{pull_resistor_1_node[4]}}, in_17}), .out(shifter_5_out));
  Pull_Resistor pull_resistor_6 (.node(shifter_5_out));
  Shifter #(.width(32)) shifter_6 (.in(in_6), .\dist ({{4{pull_resistor_1_node[4]}}, in_17}), .out(shifter_6_out));
  Pull_Resistor pull_resistor_7 (.node(shifter_6_out));
  Pull_Resistor pull_resistor_8 (.node(pull_resistor_8_node));
  Shifter #(.width(32)) shifter_7 (
    .in(in_7), .\dist ({{4{pull_resistor_1_node[4]}}, in_17}), .out(pull_resistor_8_node));
  Pull_Resistor pull_resistor_9 (.node(pull_resistor_9_node));
  Shifter #(.width(32)) shifter_8 (
    .in(in_8), .\dist ({{4{pull_resistor_1_node[4]}}, in_17}), .out(pull_resistor_9_node));
  Pull_Resistor pull_resistor_10 (.node(pull_resistor_10_node));
  Shifter #(.width(32)) shifter_9 (
    .in(in_9), .\dist ({{4{pull_resistor_1_node[4]}}, in_17}), .out(pull_resistor_10_node));
  Pull_Resistor pull_resistor_11 (.node(pull_resistor_11_node));
  Shifter #(.width(32)) shifter_10 (
    .in(in_10), .\dist ({{4{pull_resistor_1_node[4]}}, in_17}), .out(pull_resistor_11_node));
  Pull_Resistor pull_resistor_12 (.node(pull_resistor_12_node));
  Shifter #(.width(32)) shifter_11 (
    .in(in_11), .\dist ({{4{pull_resistor_1_node[4]}}, in_17}), .out(pull_resistor_12_node));
  Shifter #(.width(32)) shifter_12 (.in(in_12), .\dist ({{4{pull_resistor_1_node[4]}}, in_17}), .out(shifter_12_out));
  Pull_Resistor pull_resistor_13 (.node(shifter_12_out));
  Pull_Resistor pull_resistor_14 (.node(pull_resistor_14_node));
  Shifter #(.width(32)) shifter_13 (
    .in(in_13), .\dist ({{4{pull_resistor_1_node[4]}}, in_17}), .out(pull_resistor_14_node));
  Pull_Resistor pull_resistor_15 (.node(pull_resistor_15_node));
  Shifter #(.width(32)) shifter_14 (
    .in(in_14), .\dist ({{4{pull_resistor_1_node[4]}}, in_17}), .out(pull_resistor_15_node));
  Shifter #(.width(32)) shifter_15 (.in(in_15), .\dist ({{4{pull_resistor_1_node[4]}}, in_17}), .out(shifter_15_out));
  Pull_Resistor pull_resistor_16 (.node(shifter_15_out));
  Shifter #(.width(32)) shifter_16 (.in(in_16), .\dist ({{4{pull_resistor_1_node[4]}}, in_17}), .out(shifter_16_out));
  Pull_Resistor pull_resistor_17 (.node(shifter_16_out));
  assign out_18 = in_17 ? shifter_1_out : 32'bz;  // Controlled_Buffer controlled_buffer_1
  assign out_19 = in_17 ? shifter_2_out : 32'bz;  // Controlled_Buffer controlled_buffer_2
  assign out_20 = in_17 ? shifter_3_out : 32'bz;  // Controlled_Buffer controlled_buffer_3
  assign out_21 = in_17 ? shifter_4_out : 32'bz;  // Controlled_Buffer controlled_buffer_4
  assign out_22 = in_17 ? shifter_5_out : 32'bz;  // Controlled_Buffer controlled_buffer_5
  assign out_23 = in_17 ? shifter_6_out : 32'bz;  // Controlled_Buffer controlled_buffer_6
  assign out_24 = in_17 ? pull_resistor_8_node : 32'bz;  // Controlled_Buffer controlled_buffer_7
  assign out_25 = in_17 ? pull_resistor_9_node : 32'bz;  // Controlled_Buffer controlled_buffer_8
  assign out_26 = in_17 ? pull_resistor_10_node : 32'bz;  // Controlled_Buffer controlled_buffer_9
  assign out_27 = in_17 ? pull_resistor_11_node : 32'bz;  // Controlled_Buffer controlled_buffer_10
  assign out_28 = in_17 ? pull_resistor_12_node : 32'bz;  // Controlled_Buffer controlled_buffer_11
  assign out_29 = in_17 ? shifter_12_out : 32'bz;  // Controlled_Buffer controlled_buffer_12
  assign out_30 = in_17 ? pull_resistor_14_node : 32'bz;  // Controlled_Buffer controlled_buffer_13
  assign out_31 = in_17 ? pull_resistor_15_node : 32'bz;  // Controlled_Buffer controlled_buffer_14
  assign out_32 = in_17 ? shifter_15_out : 32'bz;  // Controlled_Buffer controlled_buffer_15
  assign out_33 = in_17 ? shifter_16_out : 32'bz;  // Controlled_Buffer controlled_buffer_16

  // Other names for the same wires on the sheet: On = in_17
endmodule

module ShifterRight (
  input  [31:0] \Вход_0 ,
  input  [31:0] in_2,
  input  [31:0] in_3,
  input  [31:0] in_4,
  input  [31:0] in_5,
  input  [31:0] in_6,
  input  [31:0] in_7,
  input  [31:0] in_8,
  input  [31:0] in_9,
  input  [31:0] in_10,
  input  [31:0] in_11,
  input  [31:0] in_12,
  input  [31:0] in_13,
  input  [31:0] in_14,
  input  [31:0] in_15,
  input  [31:0] in_16,
  input  in_17,
  output [31:0] out_18,
  output [31:0] out_19,
  output [31:0] out_20,
  output [31:0] out_21,
  output [31:0] out_22,
  output [31:0] out_23,
  output [31:0] out_24,
  output [31:0] out_25,
  output [31:0] out_26,
  output [31:0] out_27,
  output [31:0] out_28,
  output [31:0] out_29,
  output [31:0] out_30,
  output [31:0] out_31,
  output [31:0] out_32,
  output [31:0] out_33
);

  wire [4:4] pull_resistor_1_node;
  wire [31:0] pull_resistor_2_node, pull_resistor_3_node, pull_resistor_6_node, pull_resistor_8_node,
       pull_resistor_9_node, pull_resistor_10_node, pull_resistor_11_node, pull_resistor_13_node,
       pull_resistor_14_node, pull_resistor_16_node, pull_resistor_17_node, shifter_3_out, shifter_4_out,
       shifter_6_out, shifter_11_out, shifter_14_out;

  Pull_Resistor pull_resistor_1 (.node(pull_resistor_1_node[4]));
  Pull_Resistor pull_resistor_2 (.node(pull_resistor_2_node));
  Shifter #(.width(32), .shift("lr")) shifter_1 (
    .in(\Вход_0 ), .\dist ({{4{pull_resistor_1_node[4]}}, in_17}), .out(pull_resistor_2_node));
  Pull_Resistor pull_resistor_3 (.node(pull_resistor_3_node));
  Shifter #(.width(32), .shift("lr")) shifter_2 (
    .in(in_2), .\dist ({{4{pull_resistor_1_node[4]}}, in_17}), .out(pull_resistor_3_node));
  Shifter #(.width(32), .shift("lr")) shifter_3 (
    .in(in_3), .\dist ({{4{pull_resistor_1_node[4]}}, in_17}), .out(shifter_3_out));
  Pull_Resistor pull_resistor_4 (.node(shifter_3_out));
  Shifter #(.width(32), .shift("lr")) shifter_4 (
    .in(in_4), .\dist ({{4{pull_resistor_1_node[4]}}, in_17}), .out(shifter_4_out));
  Pull_Resistor pull_resistor_5 (.node(shifter_4_out));
  Pull_Resistor pull_resistor_6 (.node(pull_resistor_6_node));
  Shifter #(.width(32), .shift("lr")) shifter_5 (
    .in(in_5), .\dist ({{4{pull_resistor_1_node[4]}}, in_17}), .out(pull_resistor_6_node));
  Shifter #(.width(32), .shift("lr")) shifter_6 (
    .in(in_6), .\dist ({{4{pull_resistor_1_node[4]}}, in_17}), .out(shifter_6_out));
  Pull_Resistor pull_resistor_7 (.node(shifter_6_out));
  Pull_Resistor pull_resistor_8 (.node(pull_resistor_8_node));
  Shifter #(.width(32), .shift("lr")) shifter_7 (
    .in(in_7), .\dist ({{4{pull_resistor_1_node[4]}}, in_17}), .out(pull_resistor_8_node));
  Pull_Resistor pull_resistor_9 (.node(pull_resistor_9_node));
  Shifter #(.width(32), .shift("lr")) shifter_8 (
    .in(in_8), .\dist ({{4{pull_resistor_1_node[4]}}, in_17}), .out(pull_resistor_9_node));
  Pull_Resistor pull_resistor_10 (.node(pull_resistor_10_node));
  Shifter #(.width(32), .shift("lr")) shifter_9 (
    .in(in_9), .\dist ({{4{pull_resistor_1_node[4]}}, in_17}), .out(pull_resistor_10_node));
  Pull_Resistor pull_resistor_11 (.node(pull_resistor_11_node));
  Shifter #(.width(32), .shift("lr")) shifter_10 (
    .in(in_10), .\dist ({{4{pull_resistor_1_node[4]}}, in_17}), .out(pull_resistor_11_node));
  Shifter #(.width(32), .shift("lr")) shifter_11 (
    .in(in_11), .\dist ({{4{pull_resistor_1_node[4]}}, in_17}), .out(shifter_11_out));
  Pull_Resistor pull_resistor_12 (.node(shifter_11_out));
  Pull_Resistor pull_resistor_13 (.node(pull_resistor_13_node));
  Shifter #(.width(32), .shift("lr")) shifter_12 (
    .in(in_12), .\dist ({{4{pull_resistor_1_node[4]}}, in_17}), .out(pull_resistor_13_node));
  Pull_Resistor pull_resistor_14 (.node(pull_resistor_14_node));
  Shifter #(.width(32), .shift("lr")) shifter_13 (
    .in(in_13), .\dist ({{4{pull_resistor_1_node[4]}}, in_17}), .out(pull_resistor_14_node));
  Shifter #(.width(32), .shift("lr")) shifter_14 (
    .in(in_14), .\dist ({{4{pull_resistor_1_node[4]}}, in_17}), .out(shifter_14_out));
  Pull_Resistor pull_resistor_15 (.node(shifter_14_out));
  Pull_Resistor pull_resistor_16 (.node(pull_resistor_16_node));
  Shifter #(.width(32), .shift("lr")) shifter_15 (
    .in(in_15), .\dist ({{4{pull_resistor_1_node[4]}}, in_17}), .out(pull_resistor_16_node));
  Pull_Resistor pull_resistor_17 (.node(pull_resistor_17_node));
  Shifter #(.width(32), .shift("lr")) shifter_16 (
    .in(in_16), .\dist ({{4{pull_resistor_1_node[4]}}, in_17}), .out(pull_resistor_17_node));
  assign out_18 = in_17 ? pull_resistor_2_node : 32'bz;  // Controlled_Buffer controlled_buffer_1
  assign out_19 = in_17 ? pull_resistor_3_node : 32'bz;  // Controlled_Buffer controlled_buffer_2
  assign out_20 = in_17 ? shifter_3_out : 32'bz;  // Controlled_Buffer controlled_buffer_3
  assign out_21 = in_17 ? shifter_4_out : 32'bz;  // Controlled_Buffer controlled_buffer_4
  assign out_22 = in_17 ? pull_resistor_6_node : 32'bz;  // Controlled_Buffer controlled_buffer_5
  assign out_23 = in_17 ? shifter_6_out : 32'bz;  // Controlled_Buffer controlled_buffer_6
  assign out_24 = in_17 ? pull_resistor_8_node : 32'bz;  // Controlled_Buffer controlled_buffer_7
  assign out_25 = in_17 ? pull_resistor_9_node : 32'bz;  // Controlled_Buffer controlled_buffer_8
  assign out_26 = in_17 ? pull_resistor_10_node : 32'bz;  // Controlled_Buffer controlled_buffer_9
  assign out_27 = in_17 ? pull_resistor_11_node : 32'bz;  // Controlled_Buffer controlled_buffer_10
  assign out_28 = in_17 ? shifter_11_out : 32'bz;  // Controlled_Buffer controlled_buffer_11
  assign out_29 = in_17 ? pull_resistor_13_node : 32'bz;  // Controlled_Buffer controlled_buffer_12
  assign out_30 = in_17 ? pull_resistor_14_node : 32'bz;  // Controlled_Buffer controlled_buffer_13
  assign out_31 = in_17 ? shifter_14_out : 32'bz;  // Controlled_Buffer controlled_buffer_14
  assign out_32 = in_17 ? pull_resistor_16_node : 32'bz;  // Controlled_Buffer controlled_buffer_15
  assign out_33 = in_17 ? pull_resistor_17_node : 32'bz;  // Controlled_Buffer controlled_buffer_16

  // Other names for the same wires on the sheet: On = in_17
endmodule
